// Logisim project 16-BitSingleCycleProcessor-AbdullahCosgun-AycanDenizVit.circ as structural Verilog: 11 circuits, main circuit 16-bit Single Cycle Processor
module _16_bit_Single_Cycle_Processor (
  output [3:0] out_1,
  output [3:0] out_2,
  output [15:0] out_3,
  output [15:0] out_4,
  output [15:0] out_5,
  output [15:0] out_6,
  output [31:0] out_7
);

  wire alu_1_out_6, and_1_out, clock_out, control_unit_1_alusrc, control_unit_1_branch, control_unit_1_jump,
       control_unit_1_memread, control_unit_1_memtoreg, control_unit_1_memwrite, control_unit_1_regdst,
       control_unit_1_regwrite, reset_2_out, reset_out;
  wire [3:0] instruction_fetch_1_op, instruction_fetch_1_rd, instruction_fetch_1_shamt, multiplexer_2_out;
  wire [15:0] adder_1_output, adder_2_output, instruction_fetch_1_i_immediate,
       instruction_fetch_1_j_target_address, multiplexer_1_out, multiplexer_3_out, multiplexer_4_out,
       ram_1_data, register_1_q;

  Register #(.width(16)) register_1 (
    .D(multiplexer_1_out), .en(1'b1), .Q(register_1_q), .clk(clock_out), .clr(reset_out));
  Multiplexer #(.width(16), .enable("false")) multiplexer_1 (
    .in0(multiplexer_4_out), .in1(instruction_fetch_1_j_target_address), .out(multiplexer_1_out),
    .sel(control_unit_1_jump));
  Adder adder_1 (.Data1(register_1_q), .Data2(16'h1), .Output(adder_1_output));
  ROM #(.addrWidth(16), .dataWidth(32)) rom_1 (.addr(register_1_q), .data(out_7));  // open: sel
  Instruction_Fetch instruction_fetch_1 (
    .in_1(out_7), .rd(instruction_fetch_1_rd), .rt(out_1), .rs(out_2), .op(instruction_fetch_1_op),
    .I_immediate(instruction_fetch_1_i_immediate), .J_Target_Address(instruction_fetch_1_j_target_address),
    .shamt(instruction_fetch_1_shamt));
  Multiplexer #(.width(4), .enable("false")) multiplexer_2 (
    .in0(out_1), .in1(instruction_fetch_1_rd), .out(multiplexer_2_out), .sel(control_unit_1_regdst));
  Button reset (.out(reset_out));
  Clock clock (.out(clock_out));
  Control_Unit control_unit_1 (
    .in_1(instruction_fetch_1_op), .RegDst(control_unit_1_regdst), .ALUSrc(control_unit_1_alusrc),
    .MemToReg(control_unit_1_memtoreg), .RegWrite(control_unit_1_regwrite), .MemRead(control_unit_1_memread),
    .MemWrite(control_unit_1_memwrite), .Branch(control_unit_1_branch), .Jump(control_unit_1_jump));
  Register_File register_file_1 (
    .Write_Data(out_6), .rd(multiplexer_2_out), .reset(reset_2_out), .RegWrite(control_unit_1_regwrite),
    .rs(out_2), .rt(out_1), .data2__rt(out_3), .Clock(clock_out), .data1__rs(out_4));
  Button reset_2 (.out(reset_2_out));
  Adder adder_2 (.Data1(adder_1_output), .Data2(instruction_fetch_1_i_immediate), .Output(adder_2_output));
  Multiplexer #(.width(16), .enable("false")) multiplexer_3 (
    .in0(out_3), .in1(instruction_fetch_1_i_immediate), .out(multiplexer_3_out), .sel(control_unit_1_alusrc));
  Multiplexer #(.width(16), .enable("false")) multiplexer_4 (
    .in0(adder_1_output), .in1(adder_2_output), .out(multiplexer_4_out), .sel(and_1_out));
  and and_1 (and_1_out, control_unit_1_branch, alu_1_out_6);
  ALU alu_1 (
    .Data1(out_4), .Data2(multiplexer_3_out), .ALU_Control__from_opcode(instruction_fetch_1_op),
    .out_5(out_5), .out_6(alu_1_out_6), .Shamt(instruction_fetch_1_shamt));
  RAM #(.addrWidth(16), .dataWidth(16), .bus("separate")) ram_1 (
    .addr(out_5), .din(out_3), .data(ram_1_data), .str(control_unit_1_memwrite), .clk(clock_out),
    .ld(control_unit_1_memread));  // open: sel, clr
  Multiplexer #(.width(16), .enable("false")) multiplexer_5 (
    .in0(out_5), .in1(ram_1_data), .out(out_6), .sel(control_unit_1_memtoreg));

  // Notes on the sheet:
  //   contents of rom_1 (hex, n*v repeats v):
  //   14000001 14210002 18001080
endmodule

// HA
module Half_Adder (
  input  Data1,
  input  Data2,
  output Sum,
  output CarryOut
);

  Pull_Resistor pull_resistor_1 (.node(Data2));
  Pull_Resistor pull_resistor_2 (.node(Data1));
  xor xor_1 (Sum, Data1, Data2);
  and and_1 (CarryOut, Data1, Data2);

  // Notes on the sheet:
  //   HALF ADDER
endmodule

// FA
module Full_Adder (
  input  Data1,
  input  Data2,
  input  Cin,
  output Sum,
  output Cout
);

  wire Half_Adder_2_carryout, Half_Adder_carryout, Half_Adder_sum;

  Half_Adder Half_Adder (.Data1(Data1), .Data2(Data2), .Sum(Half_Adder_sum), .CarryOut(Half_Adder_carryout));
  Half_Adder Half_Adder_2 (.Data1(Half_Adder_sum), .Data2(Cin), .Sum(Sum), .CarryOut(Half_Adder_2_carryout));
  or or_1 (Cout, Half_Adder_2_carryout, Half_Adder_carryout);

  // Notes on the sheet:
  //   Full Adder
endmodule

// ADD
module Adder (
  input  [15:0] Data1,
  input  [15:0] Data2,
  output [15:0] Output
);

  wire full_adder_1_cout, full_adder_2_cout, full_adder_3_cout, full_adder_4_cout, full_adder_5_cout,
       full_adder_6_cout, full_adder_7_cout, full_adder_8_cout, full_adder_9_cout, full_adder_10_cout,
       full_adder_11_cout, full_adder_12_cout, full_adder_13_cout, full_adder_14_cout, full_adder_15_cout;

  Full_Adder full_adder_1 (.Data1(Data1[0]), .Data2(Data2[0]), .Cin(1'b0), .Sum(Output[0]), .Cout(full_adder_1_cout));
  Full_Adder full_adder_2 (
    .Data1(Data1[1]), .Data2(Data2[1]), .Cin(full_adder_1_cout), .Sum(Output[1]), .Cout(full_adder_2_cout));
  Full_Adder full_adder_3 (
    .Data1(Data1[2]), .Data2(Data2[2]), .Cin(full_adder_2_cout), .Sum(Output[2]), .Cout(full_adder_3_cout));
  Full_Adder full_adder_4 (
    .Data1(Data1[3]), .Data2(Data2[3]), .Cin(full_adder_3_cout), .Sum(Output[3]), .Cout(full_adder_4_cout));
  Full_Adder full_adder_5 (
    .Data1(Data1[4]), .Data2(Data2[4]), .Cin(full_adder_4_cout), .Sum(Output[4]), .Cout(full_adder_5_cout));
  Full_Adder full_adder_6 (
    .Data1(Data1[5]), .Data2(Data2[5]), .Cin(full_adder_5_cout), .Sum(Output[5]), .Cout(full_adder_6_cout));
  Full_Adder full_adder_7 (
    .Data1(Data1[6]), .Data2(Data2[6]), .Cin(full_adder_6_cout), .Sum(Output[6]), .Cout(full_adder_7_cout));
  Full_Adder full_adder_8 (
    .Data1(Data1[7]), .Data2(Data2[7]), .Cin(full_adder_7_cout), .Sum(Output[7]), .Cout(full_adder_8_cout));
  Full_Adder full_adder_9 (
    .Data1(Data1[8]), .Data2(Data2[8]), .Cin(full_adder_8_cout), .Sum(Output[8]), .Cout(full_adder_9_cout));
  Full_Adder full_adder_10 (
    .Data1(Data1[9]), .Data2(Data2[9]), .Cin(full_adder_9_cout), .Sum(Output[9]), .Cout(full_adder_10_cout));
  Full_Adder full_adder_11 (
    .Data1(Data1[10]), .Data2(Data2[10]), .Cin(full_adder_10_cout), .Sum(Output[10]),
    .Cout(full_adder_11_cout));
  Full_Adder full_adder_12 (
    .Data1(Data1[11]), .Data2(Data2[11]), .Cin(full_adder_11_cout), .Sum(Output[11]),
    .Cout(full_adder_12_cout));
  Full_Adder full_adder_13 (
    .Data1(Data1[12]), .Data2(Data2[12]), .Cin(full_adder_12_cout), .Sum(Output[12]),
    .Cout(full_adder_13_cout));
  Full_Adder full_adder_14 (
    .Data1(Data1[13]), .Data2(Data2[13]), .Cin(full_adder_13_cout), .Sum(Output[13]),
    .Cout(full_adder_14_cout));
  Full_Adder full_adder_15 (
    .Data1(Data1[14]), .Data2(Data2[14]), .Cin(full_adder_14_cout), .Sum(Output[14]),
    .Cout(full_adder_15_cout));
  Full_Adder full_adder_16 (
    .Data1(Data1[15]), .Data2(Data2[15]), .Cin(full_adder_15_cout), .Sum(Output[15]));  // open: Cout
endmodule

// SUB
module Subtractor (
  input  [15:0] Data1,
  input  [15:0] Data2,
  output [15:0] Output
);

  wire full_adder_1_cout, full_adder_2_cout, full_adder_3_cout, full_adder_4_cout, full_adder_5_cout,
       full_adder_6_cout, full_adder_7_cout, full_adder_8_cout, full_adder_9_cout, full_adder_10_cout,
       full_adder_11_cout, full_adder_12_cout, full_adder_13_cout, full_adder_14_cout, full_adder_15_cout;
  wire [15:0] not_1_out;

  assign not_1_out = ~Data2;  // NOT_Gate not_1, 16 bits wide
  Full_Adder full_adder_1 (
    .Data1(Data1[0]), .Data2(not_1_out[0]), .Cin(1'b1), .Sum(Output[0]), .Cout(full_adder_1_cout));
  Full_Adder full_adder_2 (
    .Data1(Data1[1]), .Data2(not_1_out[1]), .Cin(full_adder_1_cout), .Sum(Output[1]), .Cout(full_adder_2_cout));
  Full_Adder full_adder_3 (
    .Data1(Data1[2]), .Data2(not_1_out[2]), .Cin(full_adder_2_cout), .Sum(Output[2]), .Cout(full_adder_3_cout));
  Full_Adder full_adder_4 (
    .Data1(Data1[3]), .Data2(not_1_out[3]), .Cin(full_adder_3_cout), .Sum(Output[3]), .Cout(full_adder_4_cout));
  Full_Adder full_adder_5 (
    .Data1(Data1[4]), .Data2(not_1_out[4]), .Cin(full_adder_4_cout), .Sum(Output[4]), .Cout(full_adder_5_cout));
  Full_Adder full_adder_6 (
    .Data1(Data1[5]), .Data2(not_1_out[5]), .Cin(full_adder_5_cout), .Sum(Output[5]), .Cout(full_adder_6_cout));
  Full_Adder full_adder_7 (
    .Data1(Data1[6]), .Data2(not_1_out[6]), .Cin(full_adder_6_cout), .Sum(Output[6]), .Cout(full_adder_7_cout));
  Full_Adder full_adder_8 (
    .Data1(Data1[7]), .Data2(not_1_out[7]), .Cin(full_adder_7_cout), .Sum(Output[7]), .Cout(full_adder_8_cout));
  Full_Adder full_adder_9 (
    .Data1(Data1[8]), .Data2(not_1_out[8]), .Cin(full_adder_8_cout), .Sum(Output[8]), .Cout(full_adder_9_cout));
  Full_Adder full_adder_10 (
    .Data1(Data1[9]), .Data2(not_1_out[9]), .Cin(full_adder_9_cout), .Sum(Output[9]),
    .Cout(full_adder_10_cout));
  Full_Adder full_adder_11 (
    .Data1(Data1[10]), .Data2(not_1_out[10]), .Cin(full_adder_10_cout), .Sum(Output[10]),
    .Cout(full_adder_11_cout));
  Full_Adder full_adder_12 (
    .Data1(Data1[11]), .Data2(not_1_out[11]), .Cin(full_adder_11_cout), .Sum(Output[11]),
    .Cout(full_adder_12_cout));
  Full_Adder full_adder_13 (
    .Data1(Data1[12]), .Data2(not_1_out[12]), .Cin(full_adder_12_cout), .Sum(Output[12]),
    .Cout(full_adder_13_cout));
  Full_Adder full_adder_14 (
    .Data1(Data1[13]), .Data2(not_1_out[13]), .Cin(full_adder_13_cout), .Sum(Output[13]),
    .Cout(full_adder_14_cout));
  Full_Adder full_adder_15 (
    .Data1(Data1[14]), .Data2(not_1_out[14]), .Cin(full_adder_14_cout), .Sum(Output[14]),
    .Cout(full_adder_15_cout));
  Full_Adder full_adder_16 (
    .Data1(Data1[15]), .Data2(not_1_out[15]), .Cin(full_adder_15_cout), .Sum(Output[15]));  // open: Cout
endmodule

// MULT
module Multiplier (
  input  [15:0] Data1,
  input  [15:0] Data2,
  input  MULT,
  input  MFLO,
  input  MFHI,
  output [15:0] out_6
);

  wire clock_1_out;
  wire [15:0] controlled_buffer_1_out, controlled_buffer_2_out, Higher_q, Lower_q, multiplier_1_cout,
       multiplier_1_out;

  Clock clock_1 (.out(clock_1_out));
  Multiplier_part #(.width(16)) multiplier_1 (
    .a(Data1), .b(Data2), .out(multiplier_1_out), .cout(multiplier_1_cout));  // open: cin
  Register #(.width(16)) Lower (.D(multiplier_1_out), .en(MULT), .Q(Lower_q), .clk(clock_1_out));  // open: clr
  Register #(.width(16)) Higher (.D(multiplier_1_cout), .en(MULT), .Q(Higher_q), .clk(clock_1_out));  // open: clr
  assign controlled_buffer_1_out = MFLO ? Lower_q : 16'bz;  // Controlled_Buffer controlled_buffer_1
  assign controlled_buffer_2_out = MFHI ? Higher_q : 16'bz;  // Controlled_Buffer controlled_buffer_2
  Pull_Resistor pull_resistor_1 (.node(controlled_buffer_1_out));
  Pull_Resistor pull_resistor_2 (.node(controlled_buffer_2_out));
  assign out_6 = controlled_buffer_1_out | controlled_buffer_2_out;  // OR_Gate or_1, 16 bits wide
endmodule

// SLT
module SetLessThan (
  input  [15:0] in_1,
  input  [15:0] in_2,
  output [15:0] out_3
);

  wire comparator_1_lt;

  Comparator #(.width(16)) comparator_1 (.a(in_1), .b(in_2), .lt(comparator_1_lt));  // open: gt, eq
  assign out_3 = {{15{1'b0}}, comparator_1_lt};  // Bit_Extender bit_extender_1
endmodule

module ALU (
  input  [15:0] Data1,
  input  [15:0] Data2,
  input  [3:0] Shamt,
  input  [3:0] ALU_Control__from_opcode,
  output [15:0] out_5,
  output out_6
);

  wire comparator_1_eq, comparator_2_eq, comparator_2_lt, decoder_1_out0, decoder_1_out1, decoder_1_out2,
       decoder_1_out3, decoder_1_out4, decoder_1_out5, decoder_1_out6, decoder_1_out7, decoder_1_out8,
       decoder_1_out9, decoder_1_out12, decoder_1_out13, or_2_out;
  wire [3:0] controlled_buffer_7_out;
  wire [15:0] adder_1_output, adder_2_output, and_1_out, controlled_buffer_1_out, controlled_buffer_2_out,
       controlled_buffer_3_out, controlled_buffer_4_out, controlled_buffer_5_out, controlled_buffer_6_out,
       controlled_buffer_8_out, controlled_buffer_9_out, controlled_buffer_10_out, controlled_buffer_11_out,
       controlled_buffer_12_out, controlled_buffer_13_out, controlled_buffer_14_out,
       controlled_buffer_15_out, controlled_buffer_16_out, controlled_buffer_17_out,
       controlled_buffer_18_out, controlled_buffer_19_out, multiplier_1_out_6, or_1_out,
       pull_resistor_3_node, setlessthan_1_out_3, shifter_1_out, subtractor_1_output;

  Pull_Resistor pull_resistor_1 (.node(Data2));
  Pull_Resistor pull_resistor_2 (.node(Data1));
  Decoder #(.select(4), .enable("false")) decoder_1 (
    .out0(decoder_1_out0), .out1(decoder_1_out1), .out2(decoder_1_out2), .out3(decoder_1_out3),
    .out4(decoder_1_out4), .out5(decoder_1_out5), .out6(decoder_1_out6), .out7(decoder_1_out7),
    .out8(decoder_1_out8), .out9(decoder_1_out9), .out12(decoder_1_out12), .out13(decoder_1_out13),
    .sel(ALU_Control__from_opcode));  // open: out10, out11, out14, out15
  assign controlled_buffer_1_out = decoder_1_out12 ? Data2 : 16'bz;  // Controlled_Buffer controlled_buffer_1
  assign controlled_buffer_2_out = decoder_1_out13 ? Data1 : 16'bz;  // Controlled_Buffer controlled_buffer_2
  assign controlled_buffer_3_out = decoder_1_out4 ? Data2 : 16'bz;  // Controlled_Buffer controlled_buffer_3
  assign controlled_buffer_4_out = decoder_1_out5 ? Data1 : 16'bz;  // Controlled_Buffer controlled_buffer_4
  assign controlled_buffer_5_out = decoder_1_out5 ? Data2 : 16'bz;  // Controlled_Buffer controlled_buffer_5
  assign controlled_buffer_6_out = decoder_1_out6 ? Data1 : 16'bz;  // Controlled_Buffer controlled_buffer_6
  assign controlled_buffer_7_out = decoder_1_out6 ? Shamt : 4'bz;  // Controlled_Buffer controlled_buffer_7
  assign controlled_buffer_8_out = decoder_1_out7 ? Data1 : 16'bz;  // Controlled_Buffer controlled_buffer_8
  assign controlled_buffer_9_out = decoder_1_out7 ? Data2 : 16'bz;  // Controlled_Buffer controlled_buffer_9
  assign controlled_buffer_10_out = decoder_1_out12 ? Data1 : 16'bz;  // Controlled_Buffer controlled_buffer_10
  assign controlled_buffer_11_out = decoder_1_out0 ? Data2 : 16'bz;  // Controlled_Buffer controlled_buffer_11
  assign controlled_buffer_12_out = decoder_1_out1 ? Data1 : 16'bz;  // Controlled_Buffer controlled_buffer_12
  assign controlled_buffer_13_out = decoder_1_out1 ? Data2 : 16'bz;  // Controlled_Buffer controlled_buffer_13
  assign controlled_buffer_14_out = decoder_1_out2 ? Data1 : 16'bz;  // Controlled_Buffer controlled_buffer_14
  assign controlled_buffer_15_out = decoder_1_out2 ? Data2 : 16'bz;  // Controlled_Buffer controlled_buffer_15
  assign controlled_buffer_16_out = decoder_1_out3 ? Data1 : 16'bz;  // Controlled_Buffer controlled_buffer_16
  assign controlled_buffer_17_out = decoder_1_out3 ? Data2 : 16'bz;  // Controlled_Buffer controlled_buffer_17
  assign controlled_buffer_18_out = decoder_1_out4 ? Data1 : 16'bz;  // Controlled_Buffer controlled_buffer_18
  Pull_Resistor pull_resistor_3 (.node(pull_resistor_3_node));
  Pull_Resistor pull_resistor_4 (.node(controlled_buffer_2_out));
  assign controlled_buffer_19_out = decoder_1_out0 ? Data1 : 16'bz;  // Controlled_Buffer controlled_buffer_19
  Pull_Resistor pull_resistor_5 (.node(controlled_buffer_4_out));
  Pull_Resistor pull_resistor_6 (.node(controlled_buffer_8_out));
  Pull_Resistor pull_resistor_7 (.node(controlled_buffer_1_out));
  Pull_Resistor pull_resistor_8 (.node(controlled_buffer_6_out));
  Pull_Resistor pull_resistor_9 (.node(controlled_buffer_10_out));
  Pull_Resistor pull_resistor_10 (.node(controlled_buffer_9_out));
  Pull_Resistor pull_resistor_11 (.node(controlled_buffer_5_out));
  Pull_Resistor pull_resistor_12 (.node(controlled_buffer_7_out));
  Pull_Resistor pull_resistor_13 (.node(controlled_buffer_17_out));
  Pull_Resistor pull_resistor_14 (.node(controlled_buffer_14_out));
  Pull_Resistor pull_resistor_15 (.node(controlled_buffer_13_out));
  Pull_Resistor pull_resistor_16 (.node(controlled_buffer_3_out));
  Pull_Resistor pull_resistor_17 (.node(controlled_buffer_15_out));
  Pull_Resistor pull_resistor_18 (.node(controlled_buffer_16_out));
  Pull_Resistor pull_resistor_19 (.node(controlled_buffer_18_out));
  Pull_Resistor pull_resistor_20 (.node(controlled_buffer_12_out));
  Pull_Resistor pull_resistor_21 (.node(controlled_buffer_11_out));
  Pull_Resistor pull_resistor_22 (.node(controlled_buffer_19_out));
  Adder adder_1 (.Data1(controlled_buffer_19_out), .Data2(controlled_buffer_11_out), .Output(adder_1_output));
  Subtractor subtractor_1 (
    .Data1(controlled_buffer_12_out), .Data2(controlled_buffer_13_out), .Output(subtractor_1_output));
  assign and_1_out = controlled_buffer_16_out & controlled_buffer_17_out;  // AND_Gate and_1, 16 bits wide
  assign or_1_out = controlled_buffer_18_out | controlled_buffer_3_out;  // OR_Gate or_1, 16 bits wide
  Adder adder_2 (.Data1(controlled_buffer_4_out), .Data2(controlled_buffer_5_out), .Output(adder_2_output));
  Shifter #(.width(16)) shifter_1 (.in(controlled_buffer_6_out), .\dist (controlled_buffer_7_out), .out(shifter_1_out));
  SetLessThan setlessthan_1 (
    .in_1(controlled_buffer_8_out), .in_2(controlled_buffer_9_out), .out_3(setlessthan_1_out_3));
  Comparator #(.width(16)) comparator_1 (
    .a(controlled_buffer_10_out), .b(controlled_buffer_1_out), .eq(comparator_1_eq));  // open: gt, lt
  Comparator #(.width(16)) comparator_2 (
    .a(controlled_buffer_2_out), .b(pull_resistor_3_node), .eq(comparator_2_eq), .lt(comparator_2_lt));  // open: gt
  Multiplier multiplier_1 (
    .Data1(controlled_buffer_14_out), .Data2(controlled_buffer_15_out), .MULT(decoder_1_out2),
    .MFLO(decoder_1_out9), .MFHI(decoder_1_out8), .out_6(multiplier_1_out_6));
  or or_2 (or_2_out, comparator_2_eq, comparator_2_lt);
  assign out_5 = adder_1_output | subtractor_1_output | multiplier_1_out_6 | and_1_out | or_1_out | adder_2_output | shifter_1_out | setlessthan_1_out_3;  // OR_Gate or_3, 16 bits wide
  and and_2 (out_6, comparator_1_eq, or_2_out);
  // also tied to GND on the sheet: {pull_resistor_3_node[0], pull_resistor_3_node[1], pull_resistor_3_node[2], pull_resistor_3_node[3], pull_resistor_3_node[4], pull_resistor_3_node[5], pull_resistor_3_node[6], pull_resistor_3_node[7], pull_resistor_3_node[8], pull_resistor_3_node[9], pull_resistor_3_node[10], pull_resistor_3_node[11], pull_resistor_3_node[12], pull_resistor_3_node[13], pull_resistor_3_node[14], pull_resistor_3_node[15]}
endmodule

module Register_File (
  input  [3:0] rs,
  input  [3:0] rt,
  input  [15:0] Write_Data,
  input  [3:0] rd,
  input  reset,
  input  Clock,
  input  RegWrite,
  output [15:0] data1__rs,
  output [15:0] data2__rt
);

  wire and_1_out, and_2_out, and_3_out, and_4_out, and_5_out, and_6_out, and_7_out, and_8_out, and_9_out,
       and_10_out, and_11_out, and_12_out, and_13_out, and_14_out, and_15_out, and_16_out, decoder_1_out0,
       decoder_1_out1, decoder_1_out2, decoder_1_out3, decoder_1_out4, decoder_1_out5, decoder_1_out6,
       decoder_1_out7, decoder_1_out8, decoder_1_out9, decoder_1_out10, decoder_1_out11, decoder_1_out12,
       decoder_1_out13, decoder_1_out14, decoder_1_out15;
  wire [15:0] register_1_q, register_2_q, register_3_q, register_4_q, register_5_q, register_6_q,
       register_7_q, register_8_q, register_9_q, register_10_q, register_11_q, register_12_q, register_13_q,
       register_14_q, register_15_q, register_16_q;

  Decoder #(.select(4), .enable("false")) decoder_1 (
    .out0(decoder_1_out0), .out1(decoder_1_out1), .out2(decoder_1_out2), .out3(decoder_1_out3),
    .out4(decoder_1_out4), .out5(decoder_1_out5), .out6(decoder_1_out6), .out7(decoder_1_out7),
    .out8(decoder_1_out8), .out9(decoder_1_out9), .out10(decoder_1_out10), .out11(decoder_1_out11),
    .out12(decoder_1_out12), .out13(decoder_1_out13), .out14(decoder_1_out14), .out15(decoder_1_out15),
    .sel(rd));
  Pull_Resistor pull_resistor_1 (.node(decoder_1_out3));
  Pull_Resistor pull_resistor_2 (.node(decoder_1_out2));
  Pull_Resistor pull_resistor_3 (.node(decoder_1_out4));
  Pull_Resistor pull_resistor_4 (.node(decoder_1_out0));
  Pull_Resistor pull_resistor_5 (.node(decoder_1_out1));
  Pull_Resistor pull_resistor_6 (.node(decoder_1_out8));
  Pull_Resistor pull_resistor_7 (.node(decoder_1_out10));
  Pull_Resistor pull_resistor_8 (.node(decoder_1_out5));
  Pull_Resistor pull_resistor_9 (.node(decoder_1_out11));
  Pull_Resistor pull_resistor_10 (.node(decoder_1_out7));
  Pull_Resistor pull_resistor_11 (.node(decoder_1_out9));
  Pull_Resistor pull_resistor_12 (.node(decoder_1_out6));
  Pull_Resistor pull_resistor_13 (.node(decoder_1_out12));
  Pull_Resistor pull_resistor_14 (.node(decoder_1_out13));
  Pull_Resistor pull_resistor_15 (.node(decoder_1_out14));
  Pull_Resistor pull_resistor_16 (.node(decoder_1_out15));
  and and_1 (and_1_out, decoder_1_out0, RegWrite);
  and and_2 (and_2_out, decoder_1_out4, RegWrite);
  and and_3 (and_3_out, decoder_1_out8, RegWrite);
  and and_4 (and_4_out, decoder_1_out12, RegWrite);
  Register #(.width(16)) register_1 (.D(Write_Data), .en(and_1_out), .Q(register_1_q), .clk(Clock), .clr(reset));
  Register #(.width(16)) register_2 (.D(Write_Data), .en(and_2_out), .Q(register_2_q), .clk(Clock), .clr(reset));
  Register #(.width(16)) register_3 (.D(Write_Data), .en(and_3_out), .Q(register_3_q), .clk(Clock), .clr(reset));
  Register #(.width(16)) register_4 (.D(Write_Data), .en(and_4_out), .Q(register_4_q), .clk(Clock), .clr(reset));
  and and_5 (and_5_out, decoder_1_out1, RegWrite);
  and and_6 (and_6_out, decoder_1_out5, RegWrite);
  and and_7 (and_7_out, decoder_1_out9, RegWrite);
  and and_8 (and_8_out, decoder_1_out13, RegWrite);
  Register #(.width(16)) register_5 (.D(Write_Data), .en(and_5_out), .Q(register_5_q), .clk(Clock), .clr(reset));
  Register #(.width(16)) register_6 (.D(Write_Data), .en(and_6_out), .Q(register_6_q), .clk(Clock), .clr(reset));
  Register #(.width(16)) register_7 (.D(Write_Data), .en(and_7_out), .Q(register_7_q), .clk(Clock), .clr(reset));
  Register #(.width(16)) register_8 (.D(Write_Data), .en(and_8_out), .Q(register_8_q), .clk(Clock), .clr(reset));
  and and_9 (and_9_out, decoder_1_out2, RegWrite);
  and and_10 (and_10_out, decoder_1_out6, RegWrite);
  and and_11 (and_11_out, decoder_1_out10, RegWrite);
  and and_12 (and_12_out, decoder_1_out14, RegWrite);
  Register #(.width(16)) register_9 (.D(Write_Data), .en(and_9_out), .Q(register_9_q), .clk(Clock), .clr(reset));
  Register #(.width(16)) register_10 (.D(Write_Data), .en(and_10_out), .Q(register_10_q), .clk(Clock), .clr(reset));
  Register #(.width(16)) register_11 (.D(Write_Data), .en(and_11_out), .Q(register_11_q), .clk(Clock), .clr(reset));
  Register #(.width(16)) register_12 (.D(Write_Data), .en(and_12_out), .Q(register_12_q), .clk(Clock), .clr(reset));
  and and_13 (and_13_out, decoder_1_out3, RegWrite);
  and and_14 (and_14_out, decoder_1_out7, RegWrite);
  and and_15 (and_15_out, decoder_1_out11, RegWrite);
  and and_16 (and_16_out, decoder_1_out15, RegWrite);
  Register #(.width(16)) register_13 (.D(Write_Data), .en(and_13_out), .Q(register_13_q), .clk(Clock), .clr(reset));
  Register #(.width(16)) register_14 (.D(Write_Data), .en(and_14_out), .Q(register_14_q), .clk(Clock), .clr(reset));
  Register #(.width(16)) register_15 (.D(Write_Data), .en(and_15_out), .Q(register_15_q), .clk(Clock), .clr(reset));
  Register #(.width(16)) register_16 (.D(Write_Data), .en(and_16_out), .Q(register_16_q), .clk(Clock), .clr(reset));
  Multiplexer #(.select(4), .width(16), .enable("false")) multiplexer_1 (
    .in0(register_1_q), .in1(register_5_q), .in2(register_9_q), .in3(register_13_q), .in4(register_2_q),
    .in5(register_6_q), .in6(register_10_q), .in7(register_14_q), .in8(register_3_q), .in9(register_7_q),
    .in10(register_11_q), .in11(register_15_q), .in12(register_4_q), .in13(register_8_q),
    .in14(register_12_q), .in15(register_16_q), .out(data1__rs), .sel(rs));
  Multiplexer #(.select(4), .width(16), .enable("false")) multiplexer_2 (
    .in0(register_1_q), .in1(register_5_q), .in2(register_9_q), .in3(register_13_q), .in4(register_2_q),
    .in5(register_6_q), .in6(register_10_q), .in7(register_14_q), .in8(register_3_q), .in9(register_7_q),
    .in10(register_11_q), .in11(register_15_q), .in12(register_4_q), .in13(register_8_q),
    .in14(register_12_q), .in15(register_16_q), .out(data2__rt), .sel(rt));
endmodule

module Instruction_Fetch (
  input  [31:0] in_1,
  output [15:0] I_immediate,
  output [15:0] J_Target_Address,
  output [3:0] op,
  output [3:0] rs,
  output [3:0] rt,
  output [3:0] rd,
  output [3:0] shamt
);

  Pull_Resistor pull_resistor_1 (.node(in_1[5:0]));
  Pull_Resistor pull_resistor_2 (.node(in_1[10:6]));
  Pull_Resistor pull_resistor_3 (.node(in_1[31:26]));
  Pull_Resistor pull_resistor_4 (.node(in_1[25:21]));
  Pull_Resistor pull_resistor_5 (.node(in_1[20:16]));
  Pull_Resistor pull_resistor_6 (.node(in_1[15:11]));

  assign I_immediate = in_1[15:0];
  assign J_Target_Address = in_1[15:0];
  assign op = in_1[29:26];
  assign rd = in_1[14:11];
  assign rs = in_1[24:21];
  assign rt = in_1[19:16];
  assign shamt = in_1[9:6];

  // Notes on the sheet:
  //   We dont need these? There should be an instruction each cycle
  //   funct (not used)
endmodule

module Control_Unit (
  input  [3:0] in_1,
  output RegDst,
  output RegWrite,
  output ALUSrc,
  output MemToReg,
  output MemRead,
  output MemWrite,
  output Branch,
  output Jump
);

  wire decoder_1_out0, decoder_1_out1, decoder_1_out2, decoder_1_out3, decoder_1_out4, decoder_1_out5,
       decoder_1_out6, decoder_1_out7, decoder_1_out8, decoder_1_out9, decoder_1_out10, decoder_1_out11,
       decoder_1_out12, decoder_1_out13, decoder_1_out14, decoder_1_out15, or_1_out;
  wire [7:0] controlled_buffer_1_out, controlled_buffer_2_out, controlled_buffer_3_out,
       controlled_buffer_4_out, controlled_buffer_5_out, controlled_buffer_6_out, controlled_buffer_7_out,
       controlled_buffer_8_out, controlled_buffer_9_out;

  Decoder #(.select(4), .enable("false")) decoder_1 (
    .out0(decoder_1_out0), .out1(decoder_1_out1), .out2(decoder_1_out2), .out3(decoder_1_out3),
    .out4(decoder_1_out4), .out5(decoder_1_out5), .out6(decoder_1_out6), .out7(decoder_1_out7),
    .out8(decoder_1_out8), .out9(decoder_1_out9), .out10(decoder_1_out10), .out11(decoder_1_out11),
    .out12(decoder_1_out12), .out13(decoder_1_out13), .out14(decoder_1_out14), .out15(decoder_1_out15),
    .sel(in_1));
  assign controlled_buffer_1_out = or_1_out ? 8'h3 : 8'bz;  // Controlled_Buffer controlled_buffer_1
  or or_1 (or_1_out, decoder_1_out0, decoder_1_out1, decoder_1_out3, decoder_1_out4, decoder_1_out6, decoder_1_out7, decoder_1_out8, decoder_1_out9);
  assign controlled_buffer_2_out = decoder_1_out5 ? 8'h6 : 8'bz;  // Controlled_Buffer controlled_buffer_2
  assign controlled_buffer_3_out = decoder_1_out2 ? {8{1'b0}} : 8'bz;  // Controlled_Buffer controlled_buffer_3
  assign controlled_buffer_4_out = decoder_1_out10 ? 8'h1e : 8'bz;  // Controlled_Buffer controlled_buffer_4
  assign controlled_buffer_5_out = decoder_1_out11 ? 8'h24 : 8'bz;  // Controlled_Buffer controlled_buffer_5
  assign controlled_buffer_6_out = decoder_1_out12 ? 8'h40 : 8'bz;  // Controlled_Buffer controlled_buffer_6
  Pull_Resistor pull_resistor_1 (.node(controlled_buffer_2_out));
  Pull_Resistor pull_resistor_2 (.node(controlled_buffer_1_out));
  assign controlled_buffer_7_out = decoder_1_out13 ? 8'h40 : 8'bz;  // Controlled_Buffer controlled_buffer_7
  assign controlled_buffer_8_out = decoder_1_out14 ? 8'h80 : 8'bz;  // Controlled_Buffer controlled_buffer_8
  assign controlled_buffer_9_out = decoder_1_out15 ? 8'h44 : 8'bz;  // Controlled_Buffer controlled_buffer_9
  Pull_Resistor pull_resistor_3 (.node(controlled_buffer_8_out));
  Pull_Resistor pull_resistor_4 (.node(controlled_buffer_5_out));
  Pull_Resistor pull_resistor_5 (.node(controlled_buffer_4_out));
  Pull_Resistor pull_resistor_6 (.node(controlled_buffer_9_out));
  Pull_Resistor pull_resistor_7 (.node(controlled_buffer_6_out));
  Pull_Resistor pull_resistor_8 (.node(controlled_buffer_7_out));
  Pull_Resistor pull_resistor_9 (.node(controlled_buffer_3_out));
  assign {Jump, Branch, MemWrite, MemRead, MemToReg, ALUSrc, RegWrite, RegDst} = controlled_buffer_1_out | controlled_buffer_2_out | controlled_buffer_4_out | controlled_buffer_5_out | controlled_buffer_3_out | controlled_buffer_6_out | controlled_buffer_7_out | controlled_buffer_8_out | controlled_buffer_9_out;  // OR_Gate or_2, 8 bits wide

  // Notes on the sheet:
  //   R
  //   ADDİ
  //   LW
  //   SW
  //   BEQ
  //   BLEZ
  //   J
  //   ADDS
  //   MULT
endmodule
