// Logisim project ALU.circ as structural Verilog: 7 circuits, main circuit ALU
// HA
module Half_Adder (
  input  Data1,
  input  Data2,
  output Sum,
  output CarryOut
);

  Pull_Resistor pull_resistor_1 (.node(Data2));
  Pull_Resistor pull_resistor_2 (.node(Data1));
  xor xor_1 (Sum, Data1, Data2);
  and and_1 (CarryOut, Data1, Data2);

  // Notes on the sheet:
  //   HALF ADDER
endmodule

// FA
module Full_Adder (
  input  Data1,
  input  Data2,
  input  Cin,
  output Sum,
  output Cout
);

  wire Half_Adder_2_carryout, Half_Adder_carryout, Half_Adder_sum;

  Half_Adder Half_Adder (.Data1(Data1), .Data2(Data2), .Sum(Half_Adder_sum), .CarryOut(Half_Adder_carryout));
  Half_Adder Half_Adder_2 (.Data1(Half_Adder_sum), .Data2(Cin), .Sum(Sum), .CarryOut(Half_Adder_2_carryout));
  or or_1 (Cout, Half_Adder_2_carryout, Half_Adder_carryout);

  // Notes on the sheet:
  //   Full Adder
endmodule

// ADD
module Adder (
  input  [15:0] Data1,
  input  [15:0] Data2,
  output [15:0] Output
);

  wire full_adder_1_cout, full_adder_2_cout, full_adder_3_cout, full_adder_4_cout, full_adder_5_cout,
       full_adder_6_cout, full_adder_7_cout, full_adder_8_cout, full_adder_9_cout, full_adder_10_cout,
       full_adder_11_cout, full_adder_12_cout, full_adder_13_cout, full_adder_14_cout, full_adder_15_cout;

  Full_Adder full_adder_1 (.Data1(Data1[0]), .Data2(Data2[0]), .Cin(1'b0), .Sum(Output[0]), .Cout(full_adder_1_cout));
  Full_Adder full_adder_2 (
    .Data1(Data1[1]), .Data2(Data2[1]), .Cin(full_adder_1_cout), .Sum(Output[1]), .Cout(full_adder_2_cout));
  Full_Adder full_adder_3 (
    .Data1(Data1[2]), .Data2(Data2[2]), .Cin(full_adder_2_cout), .Sum(Output[2]), .Cout(full_adder_3_cout));
  Full_Adder full_adder_4 (
    .Data1(Data1[3]), .Data2(Data2[3]), .Cin(full_adder_3_cout), .Sum(Output[3]), .Cout(full_adder_4_cout));
  Full_Adder full_adder_5 (
    .Data1(Data1[4]), .Data2(Data2[4]), .Cin(full_adder_4_cout), .Sum(Output[4]), .Cout(full_adder_5_cout));
  Full_Adder full_adder_6 (
    .Data1(Data1[5]), .Data2(Data2[5]), .Cin(full_adder_5_cout), .Sum(Output[5]), .Cout(full_adder_6_cout));
  Full_Adder full_adder_7 (
    .Data1(Data1[6]), .Data2(Data2[6]), .Cin(full_adder_6_cout), .Sum(Output[6]), .Cout(full_adder_7_cout));
  Full_Adder full_adder_8 (
    .Data1(Data1[7]), .Data2(Data2[7]), .Cin(full_adder_7_cout), .Sum(Output[7]), .Cout(full_adder_8_cout));
  Full_Adder full_adder_9 (
    .Data1(Data1[8]), .Data2(Data2[8]), .Cin(full_adder_8_cout), .Sum(Output[8]), .Cout(full_adder_9_cout));
  Full_Adder full_adder_10 (
    .Data1(Data1[9]), .Data2(Data2[9]), .Cin(full_adder_9_cout), .Sum(Output[9]), .Cout(full_adder_10_cout));
  Full_Adder full_adder_11 (
    .Data1(Data1[10]), .Data2(Data2[10]), .Cin(full_adder_10_cout), .Sum(Output[10]),
    .Cout(full_adder_11_cout));
  Full_Adder full_adder_12 (
    .Data1(Data1[11]), .Data2(Data2[11]), .Cin(full_adder_11_cout), .Sum(Output[11]),
    .Cout(full_adder_12_cout));
  Full_Adder full_adder_13 (
    .Data1(Data1[12]), .Data2(Data2[12]), .Cin(full_adder_12_cout), .Sum(Output[12]),
    .Cout(full_adder_13_cout));
  Full_Adder full_adder_14 (
    .Data1(Data1[13]), .Data2(Data2[13]), .Cin(full_adder_13_cout), .Sum(Output[13]),
    .Cout(full_adder_14_cout));
  Full_Adder full_adder_15 (
    .Data1(Data1[14]), .Data2(Data2[14]), .Cin(full_adder_14_cout), .Sum(Output[14]),
    .Cout(full_adder_15_cout));
  Full_Adder full_adder_16 (
    .Data1(Data1[15]), .Data2(Data2[15]), .Cin(full_adder_15_cout), .Sum(Output[15]));  // open: Cout
endmodule

// SUB
module Subtractor (
  input  [15:0] Data1,
  input  [15:0] Data2,
  output [15:0] Output
);

  wire full_adder_1_cout, full_adder_2_cout, full_adder_3_cout, full_adder_4_cout, full_adder_5_cout,
       full_adder_6_cout, full_adder_7_cout, full_adder_8_cout, full_adder_9_cout, full_adder_10_cout,
       full_adder_11_cout, full_adder_12_cout, full_adder_13_cout, full_adder_14_cout, full_adder_15_cout;
  wire [15:0] not_1_out;

  assign not_1_out = ~Data2;  // NOT_Gate not_1, 16 bits wide
  Full_Adder full_adder_1 (
    .Data1(Data1[0]), .Data2(not_1_out[0]), .Cin(1'b1), .Sum(Output[0]), .Cout(full_adder_1_cout));
  Full_Adder full_adder_2 (
    .Data1(Data1[1]), .Data2(not_1_out[1]), .Cin(full_adder_1_cout), .Sum(Output[1]), .Cout(full_adder_2_cout));
  Full_Adder full_adder_3 (
    .Data1(Data1[2]), .Data2(not_1_out[2]), .Cin(full_adder_2_cout), .Sum(Output[2]), .Cout(full_adder_3_cout));
  Full_Adder full_adder_4 (
    .Data1(Data1[3]), .Data2(not_1_out[3]), .Cin(full_adder_3_cout), .Sum(Output[3]), .Cout(full_adder_4_cout));
  Full_Adder full_adder_5 (
    .Data1(Data1[4]), .Data2(not_1_out[4]), .Cin(full_adder_4_cout), .Sum(Output[4]), .Cout(full_adder_5_cout));
  Full_Adder full_adder_6 (
    .Data1(Data1[5]), .Data2(not_1_out[5]), .Cin(full_adder_5_cout), .Sum(Output[5]), .Cout(full_adder_6_cout));
  Full_Adder full_adder_7 (
    .Data1(Data1[6]), .Data2(not_1_out[6]), .Cin(full_adder_6_cout), .Sum(Output[6]), .Cout(full_adder_7_cout));
  Full_Adder full_adder_8 (
    .Data1(Data1[7]), .Data2(not_1_out[7]), .Cin(full_adder_7_cout), .Sum(Output[7]), .Cout(full_adder_8_cout));
  Full_Adder full_adder_9 (
    .Data1(Data1[8]), .Data2(not_1_out[8]), .Cin(full_adder_8_cout), .Sum(Output[8]), .Cout(full_adder_9_cout));
  Full_Adder full_adder_10 (
    .Data1(Data1[9]), .Data2(not_1_out[9]), .Cin(full_adder_9_cout), .Sum(Output[9]),
    .Cout(full_adder_10_cout));
  Full_Adder full_adder_11 (
    .Data1(Data1[10]), .Data2(not_1_out[10]), .Cin(full_adder_10_cout), .Sum(Output[10]),
    .Cout(full_adder_11_cout));
  Full_Adder full_adder_12 (
    .Data1(Data1[11]), .Data2(not_1_out[11]), .Cin(full_adder_11_cout), .Sum(Output[11]),
    .Cout(full_adder_12_cout));
  Full_Adder full_adder_13 (
    .Data1(Data1[12]), .Data2(not_1_out[12]), .Cin(full_adder_12_cout), .Sum(Output[12]),
    .Cout(full_adder_13_cout));
  Full_Adder full_adder_14 (
    .Data1(Data1[13]), .Data2(not_1_out[13]), .Cin(full_adder_13_cout), .Sum(Output[13]),
    .Cout(full_adder_14_cout));
  Full_Adder full_adder_15 (
    .Data1(Data1[14]), .Data2(not_1_out[14]), .Cin(full_adder_14_cout), .Sum(Output[14]),
    .Cout(full_adder_15_cout));
  Full_Adder full_adder_16 (
    .Data1(Data1[15]), .Data2(not_1_out[15]), .Cin(full_adder_15_cout), .Sum(Output[15]));  // open: Cout
endmodule

// MULT
module Multiplier (
  input  [15:0] Data1,
  input  [15:0] Data2,
  input  MULT,
  input  MFLO,
  input  MFHI,
  output [15:0] out_6
);

  wire clock_1_out;
  wire [15:0] controlled_buffer_1_out, controlled_buffer_2_out, Higher_q, Lower_q, multiplier_1_cout,
       multiplier_1_out;

  Clock clock_1 (.out(clock_1_out));
  Multiplier_part #(.width(16)) multiplier_1 (
    .a(Data1), .b(Data2), .out(multiplier_1_out), .cout(multiplier_1_cout));  // open: cin
  Register #(.width(16)) Lower (.D(multiplier_1_out), .en(MULT), .Q(Lower_q), .clk(clock_1_out));  // open: clr
  Register #(.width(16)) Higher (.D(multiplier_1_cout), .en(MULT), .Q(Higher_q), .clk(clock_1_out));  // open: clr
  assign controlled_buffer_1_out = MFLO ? Lower_q : 16'bz;  // Controlled_Buffer controlled_buffer_1
  assign controlled_buffer_2_out = MFHI ? Higher_q : 16'bz;  // Controlled_Buffer controlled_buffer_2
  Pull_Resistor pull_resistor_1 (.node(controlled_buffer_2_out));
  Pull_Resistor pull_resistor_2 (.node(controlled_buffer_1_out));
  assign out_6 = controlled_buffer_1_out | controlled_buffer_2_out;  // OR_Gate or_1, 16 bits wide
endmodule

// SLT
module SetLessThan (
  input  [15:0] in_1,
  input  [15:0] in_2,
  output [15:0] out_3
);

  wire comparator_1_lt;

  Comparator #(.width(16)) comparator_1 (.a(in_1), .b(in_2), .lt(comparator_1_lt));  // open: gt, eq
  assign out_3 = {{15{1'b0}}, comparator_1_lt};  // Bit_Extender bit_extender_1
endmodule

module ALU (
  input  [15:0] Data1,
  input  [15:0] Data2,
  input  [3:0] Shamt,
  input  [3:0] ALU_Control__from_opcode,
  output [15:0] out_5,
  output out_6
);

  wire comparator_1_eq, comparator_2_eq, comparator_2_lt, decoder_1_out0, decoder_1_out1, decoder_1_out2,
       decoder_1_out3, decoder_1_out4, decoder_1_out5, decoder_1_out6, decoder_1_out7, decoder_1_out8,
       decoder_1_out9, decoder_1_out10, decoder_1_out11, decoder_1_out12, decoder_1_out13, decoder_1_out15,
       or_1_out, or_3_out;
  wire [3:0] controlled_buffer_3_out;
  wire [15:0] adder_1_output, and_1_out, controlled_buffer_1_out, controlled_buffer_2_out,
       controlled_buffer_4_out, controlled_buffer_5_out, controlled_buffer_6_out, controlled_buffer_7_out,
       controlled_buffer_8_out, controlled_buffer_9_out, controlled_buffer_10_out, controlled_buffer_11_out,
       controlled_buffer_12_out, controlled_buffer_13_out, controlled_buffer_14_out,
       controlled_buffer_15_out, controlled_buffer_16_out, controlled_buffer_17_out, multiplier_1_out_6,
       or_2_out, pull_resistor_6_node, setlessthan_1_out_3, shifter_1_out, subtractor_1_output;

  Pull_Resistor pull_resistor_1 (.node(Data1));
  Pull_Resistor pull_resistor_2 (.node(Data2));
  Decoder #(.select(4), .enable("false")) decoder_1 (
    .out0(decoder_1_out0), .out1(decoder_1_out1), .out2(decoder_1_out2), .out3(decoder_1_out3),
    .out4(decoder_1_out4), .out5(decoder_1_out5), .out6(decoder_1_out6), .out7(decoder_1_out7),
    .out8(decoder_1_out8), .out9(decoder_1_out9), .out10(decoder_1_out10), .out11(decoder_1_out11),
    .out12(decoder_1_out12), .out13(decoder_1_out13), .out15(decoder_1_out15), .sel(ALU_Control__from_opcode));  // open: out14
  assign controlled_buffer_1_out = decoder_1_out4 ? Data2 : 16'bz;  // Controlled_Buffer controlled_buffer_1
  assign controlled_buffer_2_out = decoder_1_out6 ? Data1 : 16'bz;  // Controlled_Buffer controlled_buffer_2
  assign controlled_buffer_3_out = decoder_1_out6 ? Shamt : 4'bz;  // Controlled_Buffer controlled_buffer_3
  assign controlled_buffer_4_out = decoder_1_out7 ? Data1 : 16'bz;  // Controlled_Buffer controlled_buffer_4
  assign controlled_buffer_5_out = decoder_1_out7 ? Data2 : 16'bz;  // Controlled_Buffer controlled_buffer_5
  assign controlled_buffer_6_out = decoder_1_out12 ? Data1 : 16'bz;  // Controlled_Buffer controlled_buffer_6
  assign controlled_buffer_7_out = decoder_1_out12 ? Data2 : 16'bz;  // Controlled_Buffer controlled_buffer_7
  assign controlled_buffer_8_out = decoder_1_out13 ? Data1 : 16'bz;  // Controlled_Buffer controlled_buffer_8
  assign controlled_buffer_9_out = or_1_out ? Data2 : 16'bz;  // Controlled_Buffer controlled_buffer_9
  assign controlled_buffer_10_out = decoder_1_out1 ? Data1 : 16'bz;  // Controlled_Buffer controlled_buffer_10
  assign controlled_buffer_11_out = decoder_1_out1 ? Data2 : 16'bz;  // Controlled_Buffer controlled_buffer_11
  assign controlled_buffer_12_out = decoder_1_out2 ? Data1 : 16'bz;  // Controlled_Buffer controlled_buffer_12
  assign controlled_buffer_13_out = decoder_1_out2 ? Data2 : 16'bz;  // Controlled_Buffer controlled_buffer_13
  assign controlled_buffer_14_out = decoder_1_out3 ? Data1 : 16'bz;  // Controlled_Buffer controlled_buffer_14
  assign controlled_buffer_15_out = decoder_1_out3 ? Data2 : 16'bz;  // Controlled_Buffer controlled_buffer_15
  assign controlled_buffer_16_out = decoder_1_out4 ? Data1 : 16'bz;  // Controlled_Buffer controlled_buffer_16
  assign controlled_buffer_17_out = or_1_out ? Data1 : 16'bz;  // Controlled_Buffer controlled_buffer_17
  or or_1 (or_1_out, decoder_1_out0, decoder_1_out5, decoder_1_out10, decoder_1_out11, decoder_1_out15);
  Pull_Resistor pull_resistor_3 (.node(controlled_buffer_8_out));
  Pull_Resistor pull_resistor_4 (.node(controlled_buffer_2_out));
  Pull_Resistor pull_resistor_5 (.node(controlled_buffer_6_out));
  Pull_Resistor pull_resistor_6 (.node(pull_resistor_6_node));
  Pull_Resistor pull_resistor_7 (.node(controlled_buffer_5_out));
  Pull_Resistor pull_resistor_8 (.node(controlled_buffer_3_out));
  Pull_Resistor pull_resistor_9 (.node(controlled_buffer_7_out));
  Pull_Resistor pull_resistor_10 (.node(controlled_buffer_4_out));
  Pull_Resistor pull_resistor_11 (.node(controlled_buffer_13_out));
  Pull_Resistor pull_resistor_12 (.node(controlled_buffer_15_out));
  Pull_Resistor pull_resistor_13 (.node(controlled_buffer_1_out));
  Pull_Resistor pull_resistor_14 (.node(controlled_buffer_14_out));
  Pull_Resistor pull_resistor_15 (.node(controlled_buffer_16_out));
  Pull_Resistor pull_resistor_16 (.node(controlled_buffer_11_out));
  Pull_Resistor pull_resistor_17 (.node(controlled_buffer_12_out));
  Pull_Resistor pull_resistor_18 (.node(controlled_buffer_10_out));
  Pull_Resistor pull_resistor_19 (.node(controlled_buffer_9_out));
  Pull_Resistor pull_resistor_20 (.node(controlled_buffer_17_out));
  Adder adder_1 (.Data1(controlled_buffer_17_out), .Data2(controlled_buffer_9_out), .Output(adder_1_output));
  Subtractor subtractor_1 (
    .Data1(controlled_buffer_10_out), .Data2(controlled_buffer_11_out), .Output(subtractor_1_output));
  assign and_1_out = controlled_buffer_14_out & controlled_buffer_15_out;  // AND_Gate and_1, 16 bits wide
  assign or_2_out = controlled_buffer_16_out | controlled_buffer_1_out;  // OR_Gate or_2, 16 bits wide
  Shifter #(.width(16)) shifter_1 (.in(controlled_buffer_2_out), .\dist (controlled_buffer_3_out), .out(shifter_1_out));
  SetLessThan setlessthan_1 (
    .in_1(controlled_buffer_4_out), .in_2(controlled_buffer_5_out), .out_3(setlessthan_1_out_3));
  Comparator #(.width(16)) comparator_1 (
    .a(controlled_buffer_6_out), .b(controlled_buffer_7_out), .eq(comparator_1_eq));  // open: gt, lt
  Comparator #(.width(16)) comparator_2 (
    .a(controlled_buffer_8_out), .b(pull_resistor_6_node), .eq(comparator_2_eq), .lt(comparator_2_lt));  // open: gt
  Multiplier multiplier_1 (
    .Data1(controlled_buffer_12_out), .Data2(controlled_buffer_13_out), .MULT(decoder_1_out2),
    .MFLO(decoder_1_out9), .MFHI(decoder_1_out8), .out_6(multiplier_1_out_6));
  or or_3 (or_3_out, comparator_2_eq, comparator_2_lt);
  assign out_5 = adder_1_output | subtractor_1_output | multiplier_1_out_6 | and_1_out | or_2_out | shifter_1_out | setlessthan_1_out_3;  // OR_Gate or_4, 16 bits wide
  and and_2 (out_6, comparator_1_eq, or_3_out);
  // also tied to GND on the sheet: {pull_resistor_6_node[0], pull_resistor_6_node[1], pull_resistor_6_node[2], pull_resistor_6_node[3], pull_resistor_6_node[4], pull_resistor_6_node[5], pull_resistor_6_node[6], pull_resistor_6_node[7], pull_resistor_6_node[8], pull_resistor_6_node[9], pull_resistor_6_node[10], pull_resistor_6_node[11], pull_resistor_6_node[12], pull_resistor_6_node[13], pull_resistor_6_node[14], pull_resistor_6_node[15]}
endmodule
