// Logisim project Control Unit.circ as structural Verilog: 1 circuit, main circuit Control Unit
module Control_Unit (
  input  [3:0] in_1,
  output RegDst,
  output RegWrite,
  output ALUSrc,
  output ADDS,
  output MemToReg,
  output MemRead,
  output MemWrite,
  output Branch,
  output Jump
);

  wire decoder_1_out0, decoder_1_out1, decoder_1_out2, decoder_1_out3, decoder_1_out4, decoder_1_out5,
       decoder_1_out6, decoder_1_out7, decoder_1_out8, decoder_1_out9, decoder_1_out10, decoder_1_out11,
       decoder_1_out12, decoder_1_out13, decoder_1_out14, decoder_1_out15, or_1_out;
  wire [8:0] controlled_buffer_1_out, controlled_buffer_2_out, controlled_buffer_3_out,
       controlled_buffer_4_out, controlled_buffer_5_out, controlled_buffer_6_out, controlled_buffer_7_out,
       controlled_buffer_8_out, controlled_buffer_9_out;

  Decoder #(.select(4), .enable("false")) decoder_1 (
    .out0(decoder_1_out0), .out1(decoder_1_out1), .out2(decoder_1_out2), .out3(decoder_1_out3),
    .out4(decoder_1_out4), .out5(decoder_1_out5), .out6(decoder_1_out6), .out7(decoder_1_out7),
    .out8(decoder_1_out8), .out9(decoder_1_out9), .out10(decoder_1_out10), .out11(decoder_1_out11),
    .out12(decoder_1_out12), .out13(decoder_1_out13), .out14(decoder_1_out14), .out15(decoder_1_out15),
    .sel(in_1));
  assign controlled_buffer_1_out = or_1_out ? 9'h3 : 9'bz;  // Controlled_Buffer controlled_buffer_1
  or or_1 (or_1_out, decoder_1_out0, decoder_1_out1, decoder_1_out3, decoder_1_out4, decoder_1_out6, decoder_1_out7, decoder_1_out8, decoder_1_out9);
  assign controlled_buffer_2_out = decoder_1_out2 ? {9{1'b0}} : 9'bz;  // Controlled_Buffer controlled_buffer_2
  assign controlled_buffer_3_out = decoder_1_out5 ? 9'h6 : 9'bz;  // Controlled_Buffer controlled_buffer_3
  assign controlled_buffer_4_out = decoder_1_out10 ? 9'h36 : 9'bz;  // Controlled_Buffer controlled_buffer_4
  assign controlled_buffer_5_out = decoder_1_out11 ? 9'h44 : 9'bz;  // Controlled_Buffer controlled_buffer_5
  assign controlled_buffer_6_out = decoder_1_out12 ? 9'h80 : 9'bz;  // Controlled_Buffer controlled_buffer_6
  Pull_Resistor pull_resistor_1 (.node(controlled_buffer_1_out));
  assign controlled_buffer_7_out = decoder_1_out13 ? 9'h80 : 9'bz;  // Controlled_Buffer controlled_buffer_7
  assign controlled_buffer_8_out = decoder_1_out14 ? 9'h100 : 9'bz;  // Controlled_Buffer controlled_buffer_8
  assign controlled_buffer_9_out = decoder_1_out15 ? 9'h4c : 9'bz;  // Controlled_Buffer controlled_buffer_9
  Pull_Resistor pull_resistor_2 (.node(controlled_buffer_3_out));
  Pull_Resistor pull_resistor_3 (.node(controlled_buffer_2_out));
  Pull_Resistor pull_resistor_4 (.node(controlled_buffer_9_out));
  Pull_Resistor pull_resistor_5 (.node(controlled_buffer_4_out));
  Pull_Resistor pull_resistor_6 (.node(controlled_buffer_6_out));
  Pull_Resistor pull_resistor_7 (.node(controlled_buffer_5_out));
  Pull_Resistor pull_resistor_8 (.node(controlled_buffer_7_out));
  Pull_Resistor pull_resistor_9 (.node(controlled_buffer_8_out));
  assign {Jump, Branch, MemWrite, MemRead, MemToReg, ADDS, ALUSrc, RegWrite, RegDst} = controlled_buffer_1_out | controlled_buffer_2_out | controlled_buffer_3_out | controlled_buffer_4_out | controlled_buffer_5_out | controlled_buffer_6_out | controlled_buffer_7_out | controlled_buffer_8_out | controlled_buffer_9_out;  // OR_Gate or_2, 9 bits wide

  // Notes on the sheet:
  //   R
  //   MULT
  //   ADDİ
  //   LW
  //   SW
  //   BEQ
  //   BLEZ
  //   J
  //   ADDS
endmodule
