// Logisim project Instruction Fetch.circ as structural Verilog: 1 circuit, main circuit Instruction Fetch
module Instruction_Fetch (
  input  [31:0] in_1,
  output [15:0] I_immediate,
  output [15:0] J_Target_Address,
  output [3:0] op,
  output [3:0] rs,
  output [3:0] rt,
  output [3:0] rd,
  output [3:0] shamt
);


  assign I_immediate = in_1[15:0];
  assign J_Target_Address = in_1[15:0];
  assign op = in_1[29:26];
  assign rd = in_1[14:11];
  assign rs = in_1[24:21];
  assign rt = in_1[19:16];
  assign shamt = in_1[9:6];

  // Notes on the sheet:
  //   funct (not used)
endmodule
