// Logisim project MultiplierSubBlock.circ as structural Verilog: 1 circuit, main circuit Multiplier
// MULT
module Multiplier (
  input  [15:0] Data1,
  input  [15:0] Data2,
  input  MULT,
  input  MFLO,
  input  MFHI,
  output [15:0] out_6
);

  wire clock_1_out;
  wire [15:0] controlled_buffer_1_out, controlled_buffer_2_out, Higher_q, Lower_q, multiplier_1_cout,
       multiplier_1_out;

  Clock clock_1 (.out(clock_1_out));
  Multiplier_part #(.width(16)) multiplier_1 (
    .a(Data1), .b(Data2), .out(multiplier_1_out), .cout(multiplier_1_cout));  // open: cin
  Register #(.width(16)) Lower (.D(multiplier_1_out), .en(MULT), .Q(Lower_q), .clk(clock_1_out));  // open: clr
  Register #(.width(16)) Higher (.D(multiplier_1_cout), .en(MULT), .Q(Higher_q), .clk(clock_1_out));  // open: clr
  assign controlled_buffer_1_out = MFLO ? Lower_q : 16'bz;  // Controlled_Buffer controlled_buffer_1
  assign controlled_buffer_2_out = MFHI ? Higher_q : 16'bz;  // Controlled_Buffer controlled_buffer_2
  Pull_Resistor pull_resistor_1 (.node(controlled_buffer_1_out));
  Pull_Resistor pull_resistor_2 (.node(controlled_buffer_2_out));
  assign out_6 = controlled_buffer_1_out | controlled_buffer_2_out;  // OR_Gate or_1, 16 bits wide
endmodule
