// Logisim project SetLessThanSubBlock.circ as structural Verilog: 1 circuit, main circuit SetLessThan
// SLT
module SetLessThan (
  input  [15:0] in_1,
  input  [15:0] in_2,
  output [15:0] out_3
);

  wire comparator_1_lt;

  Comparator #(.width(16)) comparator_1 (.a(in_1), .b(in_2), .lt(comparator_1_lt));  // open: gt, eq
  assign out_3 = {{15{1'b0}}, comparator_1_lt};  // Bit_Extender bit_extender_1
endmodule
