// Logisim project adderSubBlocks.circ as structural Verilog: 4 circuits, main circuit Half Adder
// HA
module Half_Adder (
  input  Data1,
  input  Data2,
  output Sum,
  output CarryOut
);

  Pull_Resistor pull_resistor_1 (.node(Data2));
  Pull_Resistor pull_resistor_2 (.node(Data1));
  xor xor_1 (Sum, Data1, Data2);
  and and_1 (CarryOut, Data1, Data2);

  // Notes on the sheet:
  //   HALF ADDER
endmodule

// FA
module Full_Adder (
  input  Data1,
  input  Data2,
  input  Cin,
  output Sum,
  output Cout
);

  wire Half_Adder_2_carryout, Half_Adder_carryout, Half_Adder_sum;

  Half_Adder Half_Adder (.Data1(Data1), .Data2(Data2), .Sum(Half_Adder_sum), .CarryOut(Half_Adder_carryout));
  Half_Adder Half_Adder_2 (.Data1(Half_Adder_sum), .Data2(Cin), .Sum(Sum), .CarryOut(Half_Adder_2_carryout));
  or or_1 (Cout, Half_Adder_2_carryout, Half_Adder_carryout);

  // Notes on the sheet:
  //   Full Adder
endmodule

// ADD
module Adder (
  input  [15:0] Data1,
  input  [15:0] Data2,
  output [15:0] Output
);

  wire full_adder_1_cout, full_adder_2_cout, full_adder_3_cout, full_adder_4_cout, full_adder_5_cout,
       full_adder_6_cout, full_adder_7_cout, full_adder_8_cout, full_adder_9_cout, full_adder_10_cout,
       full_adder_11_cout, full_adder_12_cout, full_adder_13_cout, full_adder_14_cout, full_adder_15_cout;

  Full_Adder full_adder_1 (.Data1(Data1[0]), .Data2(Data2[0]), .Cin(1'b0), .Sum(Output[0]), .Cout(full_adder_1_cout));
  Full_Adder full_adder_2 (
    .Data1(Data1[1]), .Data2(Data2[1]), .Cin(full_adder_1_cout), .Sum(Output[1]), .Cout(full_adder_2_cout));
  Full_Adder full_adder_3 (
    .Data1(Data1[2]), .Data2(Data2[2]), .Cin(full_adder_2_cout), .Sum(Output[2]), .Cout(full_adder_3_cout));
  Full_Adder full_adder_4 (
    .Data1(Data1[3]), .Data2(Data2[3]), .Cin(full_adder_3_cout), .Sum(Output[3]), .Cout(full_adder_4_cout));
  Full_Adder full_adder_5 (
    .Data1(Data1[4]), .Data2(Data2[4]), .Cin(full_adder_4_cout), .Sum(Output[4]), .Cout(full_adder_5_cout));
  Full_Adder full_adder_6 (
    .Data1(Data1[5]), .Data2(Data2[5]), .Cin(full_adder_5_cout), .Sum(Output[5]), .Cout(full_adder_6_cout));
  Full_Adder full_adder_7 (
    .Data1(Data1[6]), .Data2(Data2[6]), .Cin(full_adder_6_cout), .Sum(Output[6]), .Cout(full_adder_7_cout));
  Full_Adder full_adder_8 (
    .Data1(Data1[7]), .Data2(Data2[7]), .Cin(full_adder_7_cout), .Sum(Output[7]), .Cout(full_adder_8_cout));
  Full_Adder full_adder_9 (
    .Data1(Data1[8]), .Data2(Data2[8]), .Cin(full_adder_8_cout), .Sum(Output[8]), .Cout(full_adder_9_cout));
  Full_Adder full_adder_10 (
    .Data1(Data1[9]), .Data2(Data2[9]), .Cin(full_adder_9_cout), .Sum(Output[9]), .Cout(full_adder_10_cout));
  Full_Adder full_adder_11 (
    .Data1(Data1[10]), .Data2(Data2[10]), .Cin(full_adder_10_cout), .Sum(Output[10]),
    .Cout(full_adder_11_cout));
  Full_Adder full_adder_12 (
    .Data1(Data1[11]), .Data2(Data2[11]), .Cin(full_adder_11_cout), .Sum(Output[11]),
    .Cout(full_adder_12_cout));
  Full_Adder full_adder_13 (
    .Data1(Data1[12]), .Data2(Data2[12]), .Cin(full_adder_12_cout), .Sum(Output[12]),
    .Cout(full_adder_13_cout));
  Full_Adder full_adder_14 (
    .Data1(Data1[13]), .Data2(Data2[13]), .Cin(full_adder_13_cout), .Sum(Output[13]),
    .Cout(full_adder_14_cout));
  Full_Adder full_adder_15 (
    .Data1(Data1[14]), .Data2(Data2[14]), .Cin(full_adder_14_cout), .Sum(Output[14]),
    .Cout(full_adder_15_cout));
  Full_Adder full_adder_16 (
    .Data1(Data1[15]), .Data2(Data2[15]), .Cin(full_adder_15_cout), .Sum(Output[15]));  // open: Cout
endmodule

// SUB
module Subtractor (
  input  [15:0] Data1,
  input  [15:0] Data2,
  output [15:0] Output
);

  wire full_adder_1_cout, full_adder_2_cout, full_adder_3_cout, full_adder_4_cout, full_adder_5_cout,
       full_adder_6_cout, full_adder_7_cout, full_adder_8_cout, full_adder_9_cout, full_adder_10_cout,
       full_adder_11_cout, full_adder_12_cout, full_adder_13_cout, full_adder_14_cout, full_adder_15_cout;
  wire [15:0] not_1_out;

  assign not_1_out = ~Data2;  // NOT_Gate not_1, 16 bits wide
  Full_Adder full_adder_1 (
    .Data1(Data1[0]), .Data2(not_1_out[0]), .Cin(1'b1), .Sum(Output[0]), .Cout(full_adder_1_cout));
  Full_Adder full_adder_2 (
    .Data1(Data1[1]), .Data2(not_1_out[1]), .Cin(full_adder_1_cout), .Sum(Output[1]), .Cout(full_adder_2_cout));
  Full_Adder full_adder_3 (
    .Data1(Data1[2]), .Data2(not_1_out[2]), .Cin(full_adder_2_cout), .Sum(Output[2]), .Cout(full_adder_3_cout));
  Full_Adder full_adder_4 (
    .Data1(Data1[3]), .Data2(not_1_out[3]), .Cin(full_adder_3_cout), .Sum(Output[3]), .Cout(full_adder_4_cout));
  Full_Adder full_adder_5 (
    .Data1(Data1[4]), .Data2(not_1_out[4]), .Cin(full_adder_4_cout), .Sum(Output[4]), .Cout(full_adder_5_cout));
  Full_Adder full_adder_6 (
    .Data1(Data1[5]), .Data2(not_1_out[5]), .Cin(full_adder_5_cout), .Sum(Output[5]), .Cout(full_adder_6_cout));
  Full_Adder full_adder_7 (
    .Data1(Data1[6]), .Data2(not_1_out[6]), .Cin(full_adder_6_cout), .Sum(Output[6]), .Cout(full_adder_7_cout));
  Full_Adder full_adder_8 (
    .Data1(Data1[7]), .Data2(not_1_out[7]), .Cin(full_adder_7_cout), .Sum(Output[7]), .Cout(full_adder_8_cout));
  Full_Adder full_adder_9 (
    .Data1(Data1[8]), .Data2(not_1_out[8]), .Cin(full_adder_8_cout), .Sum(Output[8]), .Cout(full_adder_9_cout));
  Full_Adder full_adder_10 (
    .Data1(Data1[9]), .Data2(not_1_out[9]), .Cin(full_adder_9_cout), .Sum(Output[9]),
    .Cout(full_adder_10_cout));
  Full_Adder full_adder_11 (
    .Data1(Data1[10]), .Data2(not_1_out[10]), .Cin(full_adder_10_cout), .Sum(Output[10]),
    .Cout(full_adder_11_cout));
  Full_Adder full_adder_12 (
    .Data1(Data1[11]), .Data2(not_1_out[11]), .Cin(full_adder_11_cout), .Sum(Output[11]),
    .Cout(full_adder_12_cout));
  Full_Adder full_adder_13 (
    .Data1(Data1[12]), .Data2(not_1_out[12]), .Cin(full_adder_12_cout), .Sum(Output[12]),
    .Cout(full_adder_13_cout));
  Full_Adder full_adder_14 (
    .Data1(Data1[13]), .Data2(not_1_out[13]), .Cin(full_adder_13_cout), .Sum(Output[13]),
    .Cout(full_adder_14_cout));
  Full_Adder full_adder_15 (
    .Data1(Data1[14]), .Data2(not_1_out[14]), .Cin(full_adder_14_cout), .Sum(Output[14]),
    .Cout(full_adder_15_cout));
  Full_Adder full_adder_16 (
    .Data1(Data1[15]), .Data2(not_1_out[15]), .Cin(full_adder_15_cout), .Sum(Output[15]));  // open: Cout
endmodule
