// Logisim project project.circ as structural Verilog: 9 circuits, main circuit 16-bit Single Cycle Processor
module _16_bit_Single_Cycle_Processor (
  input  [4:0] in_1,
  input  [4:0] in_2,
  input  [4:0] in_3,
  input  [15:0] in_4,
  input  [3:0] in_5,
  input  regWrite,
  output [15:0] out_7,
  output [15:0] out_8,
  output [15:0] out_9
);

  wire clock_out, reset_out;

  Button reset (.out(reset_out));
  Clock clock (.out(clock_out));
  Register_File register_file_1 (
    .Write_Data(in_4), .rd(in_3), .reset(reset_out), .RegWrite(regWrite), .rs(in_1), .rt(in_2),
    .data1__rs(out_9), .data2__rt(out_8), .Clock(clock_out));
  ALU alu_1 (.Data1(out_9), .Data2(out_8), .ALU_Control__from_opcode(in_5), .out_5(out_7), .CLK(clock_out));
endmodule

// HA
module Half_Adder (
  input  Data1,
  input  Data2,
  output Sum,
  output CarryOut
);

  Pull_Resistor pull_resistor_1 (.node(Data2));
  Pull_Resistor pull_resistor_2 (.node(Data1));
  xor xor_1 (Sum, Data1, Data2);
  and and_1 (CarryOut, Data1, Data2);

  // Notes on the sheet:
  //   HALF ADDER
endmodule

// FA
module Full_Adder (
  input  Data1,
  input  Data2,
  input  Cin,
  output Sum,
  output Cout
);

  wire Half_Adder_2_carryout, Half_Adder_carryout, Half_Adder_sum;

  Half_Adder Half_Adder (.Data1(Data1), .Data2(Data2), .Sum(Half_Adder_sum), .CarryOut(Half_Adder_carryout));
  Half_Adder Half_Adder_2 (.Data1(Half_Adder_sum), .Data2(Cin), .Sum(Sum), .CarryOut(Half_Adder_2_carryout));
  or or_1 (Cout, Half_Adder_2_carryout, Half_Adder_carryout);

  // Notes on the sheet:
  //   Full Adder
endmodule

// Add
module Adder (
  input  [15:0] Data1,
  input  [15:0] Data2,
  output [15:0] Output
);

  wire full_adder_1_cout, full_adder_2_cout, full_adder_3_cout, full_adder_4_cout, full_adder_5_cout,
       full_adder_6_cout, full_adder_7_cout, full_adder_8_cout, full_adder_9_cout, full_adder_10_cout,
       full_adder_11_cout, full_adder_12_cout, full_adder_13_cout, full_adder_14_cout, full_adder_15_cout;

  Full_Adder full_adder_1 (.Data1(Data1[0]), .Data2(Data2[0]), .Cin(1'b0), .Sum(Output[0]), .Cout(full_adder_1_cout));
  Full_Adder full_adder_2 (
    .Data1(Data1[1]), .Data2(Data2[1]), .Cin(full_adder_1_cout), .Sum(Output[1]), .Cout(full_adder_2_cout));
  Full_Adder full_adder_3 (
    .Data1(Data1[2]), .Data2(Data2[2]), .Cin(full_adder_2_cout), .Sum(Output[2]), .Cout(full_adder_3_cout));
  Full_Adder full_adder_4 (
    .Data1(Data1[3]), .Data2(Data2[3]), .Cin(full_adder_3_cout), .Sum(Output[3]), .Cout(full_adder_4_cout));
  Full_Adder full_adder_5 (
    .Data1(Data1[4]), .Data2(Data2[4]), .Cin(full_adder_4_cout), .Sum(Output[4]), .Cout(full_adder_5_cout));
  Full_Adder full_adder_6 (
    .Data1(Data1[5]), .Data2(Data2[5]), .Cin(full_adder_5_cout), .Sum(Output[5]), .Cout(full_adder_6_cout));
  Full_Adder full_adder_7 (
    .Data1(Data1[6]), .Data2(Data2[6]), .Cin(full_adder_6_cout), .Sum(Output[6]), .Cout(full_adder_7_cout));
  Full_Adder full_adder_8 (
    .Data1(Data1[7]), .Data2(Data2[7]), .Cin(full_adder_7_cout), .Sum(Output[7]), .Cout(full_adder_8_cout));
  Full_Adder full_adder_9 (
    .Data1(Data1[8]), .Data2(Data2[8]), .Cin(full_adder_8_cout), .Sum(Output[8]), .Cout(full_adder_9_cout));
  Full_Adder full_adder_10 (
    .Data1(Data1[9]), .Data2(Data2[9]), .Cin(full_adder_9_cout), .Sum(Output[9]), .Cout(full_adder_10_cout));
  Full_Adder full_adder_11 (
    .Data1(Data1[10]), .Data2(Data2[10]), .Cin(full_adder_10_cout), .Sum(Output[10]),
    .Cout(full_adder_11_cout));
  Full_Adder full_adder_12 (
    .Data1(Data1[11]), .Data2(Data2[11]), .Cin(full_adder_11_cout), .Sum(Output[11]),
    .Cout(full_adder_12_cout));
  Full_Adder full_adder_13 (
    .Data1(Data1[12]), .Data2(Data2[12]), .Cin(full_adder_12_cout), .Sum(Output[12]),
    .Cout(full_adder_13_cout));
  Full_Adder full_adder_14 (
    .Data1(Data1[13]), .Data2(Data2[13]), .Cin(full_adder_13_cout), .Sum(Output[13]),
    .Cout(full_adder_14_cout));
  Full_Adder full_adder_15 (
    .Data1(Data1[14]), .Data2(Data2[14]), .Cin(full_adder_14_cout), .Sum(Output[14]),
    .Cout(full_adder_15_cout));
  Full_Adder full_adder_16 (
    .Data1(Data1[15]), .Data2(Data2[15]), .Cin(full_adder_15_cout), .Sum(Output[15]));  // open: Cout
endmodule

// Sub
module Subtractor (
  input  [15:0] Data1,
  input  [15:0] Data2,
  output [15:0] Output
);

  wire full_adder_1_cout, full_adder_2_cout, full_adder_3_cout, full_adder_4_cout, full_adder_5_cout,
       full_adder_6_cout, full_adder_7_cout, full_adder_8_cout, full_adder_9_cout, full_adder_10_cout,
       full_adder_11_cout, full_adder_12_cout, full_adder_13_cout, full_adder_14_cout, full_adder_15_cout;
  wire [15:0] not_1_out;

  assign not_1_out = ~Data2;  // NOT_Gate not_1, 16 bits wide
  Full_Adder full_adder_1 (
    .Data1(Data1[0]), .Data2(not_1_out[0]), .Cin(1'b1), .Sum(Output[0]), .Cout(full_adder_1_cout));
  Full_Adder full_adder_2 (
    .Data1(Data1[1]), .Data2(not_1_out[1]), .Cin(full_adder_1_cout), .Sum(Output[1]), .Cout(full_adder_2_cout));
  Full_Adder full_adder_3 (
    .Data1(Data1[2]), .Data2(not_1_out[2]), .Cin(full_adder_2_cout), .Sum(Output[2]), .Cout(full_adder_3_cout));
  Full_Adder full_adder_4 (
    .Data1(Data1[3]), .Data2(not_1_out[3]), .Cin(full_adder_3_cout), .Sum(Output[3]), .Cout(full_adder_4_cout));
  Full_Adder full_adder_5 (
    .Data1(Data1[4]), .Data2(not_1_out[4]), .Cin(full_adder_4_cout), .Sum(Output[4]), .Cout(full_adder_5_cout));
  Full_Adder full_adder_6 (
    .Data1(Data1[5]), .Data2(not_1_out[5]), .Cin(full_adder_5_cout), .Sum(Output[5]), .Cout(full_adder_6_cout));
  Full_Adder full_adder_7 (
    .Data1(Data1[6]), .Data2(not_1_out[6]), .Cin(full_adder_6_cout), .Sum(Output[6]), .Cout(full_adder_7_cout));
  Full_Adder full_adder_8 (
    .Data1(Data1[7]), .Data2(not_1_out[7]), .Cin(full_adder_7_cout), .Sum(Output[7]), .Cout(full_adder_8_cout));
  Full_Adder full_adder_9 (
    .Data1(Data1[8]), .Data2(not_1_out[8]), .Cin(full_adder_8_cout), .Sum(Output[8]), .Cout(full_adder_9_cout));
  Full_Adder full_adder_10 (
    .Data1(Data1[9]), .Data2(not_1_out[9]), .Cin(full_adder_9_cout), .Sum(Output[9]),
    .Cout(full_adder_10_cout));
  Full_Adder full_adder_11 (
    .Data1(Data1[10]), .Data2(not_1_out[10]), .Cin(full_adder_10_cout), .Sum(Output[10]),
    .Cout(full_adder_11_cout));
  Full_Adder full_adder_12 (
    .Data1(Data1[11]), .Data2(not_1_out[11]), .Cin(full_adder_11_cout), .Sum(Output[11]),
    .Cout(full_adder_12_cout));
  Full_Adder full_adder_13 (
    .Data1(Data1[12]), .Data2(not_1_out[12]), .Cin(full_adder_12_cout), .Sum(Output[12]),
    .Cout(full_adder_13_cout));
  Full_Adder full_adder_14 (
    .Data1(Data1[13]), .Data2(not_1_out[13]), .Cin(full_adder_13_cout), .Sum(Output[13]),
    .Cout(full_adder_14_cout));
  Full_Adder full_adder_15 (
    .Data1(Data1[14]), .Data2(not_1_out[14]), .Cin(full_adder_14_cout), .Sum(Output[14]),
    .Cout(full_adder_15_cout));
  Full_Adder full_adder_16 (
    .Data1(Data1[15]), .Data2(not_1_out[15]), .Cin(full_adder_15_cout), .Sum(Output[15]));  // open: Cout
endmodule

module Multiplier (
  input  [15:0] Data1,
  input  [15:0] Data2,
  input  MULT,
  input  MFLO,
  input  MFHI,
  output [15:0] out_6
);

  wire [15:0] controlled_buffer_1_out, controlled_buffer_2_out, Higher_q, Lower_q, multiplier_1_cout,
       multiplier_1_out;

  Multiplier_part #(.width(16)) multiplier_1 (
    .a(Data1), .b(Data2), .out(multiplier_1_out), .cout(multiplier_1_cout));  // open: cin
  Register #(.width(16)) Lower (.D(multiplier_1_out), .en(MULT), .Q(Lower_q), .clk(MULT));  // open: clr
  Register #(.width(16)) Higher (.D(multiplier_1_cout), .en(MULT), .Q(Higher_q), .clk(MULT));  // open: clr
  assign controlled_buffer_1_out = MFLO ? Lower_q : 16'bz;  // Controlled_Buffer controlled_buffer_1
  assign controlled_buffer_2_out = MFHI ? Higher_q : 16'bz;  // Controlled_Buffer controlled_buffer_2
  Pull_Resistor pull_resistor_1 (.node(controlled_buffer_2_out));
  Pull_Resistor pull_resistor_2 (.node(controlled_buffer_1_out));
  assign out_6 = controlled_buffer_1_out | controlled_buffer_2_out;  // OR_Gate or_1, 16 bits wide
endmodule

// SLT
module SetLessThan (
  input  [15:0] in_1,
  input  [15:0] in_2,
  output [15:0] out_3
);

  wire comparator_1_lt;

  Comparator #(.width(16)) comparator_1 (.a(in_1), .b(in_2), .lt(comparator_1_lt));  // open: gt, eq
  assign out_3 = {{15{1'b0}}, comparator_1_lt};  // Bit_Extender bit_extender_1
endmodule

module ALU (
  input  [15:0] Data1,
  input  [15:0] Data2,
  input  CLK,
  input  [3:0] ALU_Control__from_opcode,
  output [15:0] out_5
);

  wire and_1_out, demultiplexer_1_out0, demultiplexer_1_out1, demultiplexer_1_out2, demultiplexer_1_out3,
       demultiplexer_1_out4, demultiplexer_1_out5, demultiplexer_1_out6, demultiplexer_1_out7,
       demultiplexer_1_out8, demultiplexer_1_out9;
  wire [3:0] controlled_buffer_5_out;
  wire [15:0] add_output, addi_output, and_2_out, controlled_buffer_1_out, controlled_buffer_2_out,
       controlled_buffer_3_out, controlled_buffer_4_out, controlled_buffer_6_out, controlled_buffer_7_out,
       controlled_buffer_8_out, controlled_buffer_9_out, controlled_buffer_10_out, controlled_buffer_11_out,
       controlled_buffer_12_out, controlled_buffer_13_out, controlled_buffer_14_out,
       controlled_buffer_15_out, controlled_buffer_16_out, multiplier_1_out_6, or_1_out, setlessthan_1_out_3,
       shifter_1_out, subtractor_1_output;

  Pull_Resistor pull_resistor_1 (.node(Data1));
  Pull_Resistor pull_resistor_2 (.node(Data2));
  Demultiplexer #(.select(4), .enable("false")) demultiplexer_1 (
    .out0(demultiplexer_1_out0), .out1(demultiplexer_1_out1), .out2(demultiplexer_1_out2),
    .out3(demultiplexer_1_out3), .out4(demultiplexer_1_out4), .out5(demultiplexer_1_out5),
    .out6(demultiplexer_1_out6), .out7(demultiplexer_1_out7), .out8(demultiplexer_1_out8),
    .out9(demultiplexer_1_out9), .in(1'b1), .sel(ALU_Control__from_opcode));  // open: out10, out11, out12, out13, out14, out15
  assign controlled_buffer_1_out = demultiplexer_1_out4 ? Data2 : 16'bz;  // Controlled_Buffer controlled_buffer_1
  assign controlled_buffer_2_out = demultiplexer_1_out5 ? Data1 : 16'bz;  // Controlled_Buffer controlled_buffer_2
  assign controlled_buffer_3_out = demultiplexer_1_out5 ? Data2 : 16'bz;  // Controlled_Buffer controlled_buffer_3
  assign controlled_buffer_4_out = demultiplexer_1_out6 ? Data1 : 16'bz;  // Controlled_Buffer controlled_buffer_4
  assign controlled_buffer_5_out = demultiplexer_1_out6 ? Data2[3:0] : 4'bz;  // Controlled_Buffer controlled_buffer_5
  assign controlled_buffer_6_out = demultiplexer_1_out7 ? Data1 : 16'bz;  // Controlled_Buffer controlled_buffer_6
  assign controlled_buffer_7_out = demultiplexer_1_out7 ? Data2 : 16'bz;  // Controlled_Buffer controlled_buffer_7
  assign controlled_buffer_8_out = demultiplexer_1_out0 ? Data2 : 16'bz;  // Controlled_Buffer controlled_buffer_8
  assign controlled_buffer_9_out = demultiplexer_1_out1 ? Data1 : 16'bz;  // Controlled_Buffer controlled_buffer_9
  assign controlled_buffer_10_out = demultiplexer_1_out1 ? Data2 : 16'bz;  // Controlled_Buffer controlled_buffer_10
  assign controlled_buffer_11_out = demultiplexer_1_out2 ? Data1 : 16'bz;  // Controlled_Buffer controlled_buffer_11
  assign controlled_buffer_12_out = demultiplexer_1_out2 ? Data2 : 16'bz;  // Controlled_Buffer controlled_buffer_12
  assign controlled_buffer_13_out = demultiplexer_1_out3 ? Data1 : 16'bz;  // Controlled_Buffer controlled_buffer_13
  assign controlled_buffer_14_out = demultiplexer_1_out3 ? Data2 : 16'bz;  // Controlled_Buffer controlled_buffer_14
  assign controlled_buffer_15_out = demultiplexer_1_out4 ? Data1 : 16'bz;  // Controlled_Buffer controlled_buffer_15
  assign controlled_buffer_16_out = demultiplexer_1_out0 ? Data1 : 16'bz;  // Controlled_Buffer controlled_buffer_16
  and and_1 (and_1_out, CLK, demultiplexer_1_out7);
  Pull_Resistor pull_resistor_3 (.node(controlled_buffer_7_out));
  Pull_Resistor pull_resistor_4 (.node(controlled_buffer_2_out));
  Pull_Resistor pull_resistor_5 (.node(controlled_buffer_3_out));
  Pull_Resistor pull_resistor_6 (.node(controlled_buffer_5_out));
  Pull_Resistor pull_resistor_7 (.node(controlled_buffer_6_out));
  Pull_Resistor pull_resistor_8 (.node(controlled_buffer_4_out));
  Pull_Resistor pull_resistor_9 (.node(controlled_buffer_9_out));
  Pull_Resistor pull_resistor_10 (.node(controlled_buffer_14_out));
  Pull_Resistor pull_resistor_11 (.node(controlled_buffer_10_out));
  Pull_Resistor pull_resistor_12 (.node(controlled_buffer_11_out));
  Pull_Resistor pull_resistor_13 (.node(controlled_buffer_13_out));
  Pull_Resistor pull_resistor_14 (.node(controlled_buffer_12_out));
  Pull_Resistor pull_resistor_15 (.node(controlled_buffer_15_out));
  Pull_Resistor pull_resistor_16 (.node(controlled_buffer_1_out));
  Pull_Resistor pull_resistor_17 (.node(controlled_buffer_16_out));
  Pull_Resistor pull_resistor_18 (.node(controlled_buffer_8_out));
  Adder add (.Data1(controlled_buffer_16_out), .Data2(controlled_buffer_8_out), .Output(add_output));
  Subtractor subtractor_1 (
    .Data1(controlled_buffer_9_out), .Data2(controlled_buffer_10_out), .Output(subtractor_1_output));
  SetLessThan setlessthan_1 (
    .in_1(controlled_buffer_11_out), .in_2(controlled_buffer_12_out), .out_3(setlessthan_1_out_3));
  assign and_2_out = controlled_buffer_13_out & controlled_buffer_14_out;  // AND_Gate and_2, 16 bits wide
  assign or_1_out = controlled_buffer_15_out | controlled_buffer_1_out;  // OR_Gate or_1, 16 bits wide
  Adder addi (.Data1(controlled_buffer_2_out), .Data2(controlled_buffer_3_out), .Output(addi_output));
  Shifter #(.width(16)) shifter_1 (.in(controlled_buffer_4_out), .\dist (controlled_buffer_5_out), .out(shifter_1_out));
  Multiplier multiplier_1 (
    .Data1(controlled_buffer_6_out), .Data2(controlled_buffer_7_out), .MULT(and_1_out),
    .MFLO(demultiplexer_1_out8), .MFHI(demultiplexer_1_out9), .out_6(multiplier_1_out_6));
  assign out_5 = add_output | subtractor_1_output | setlessthan_1_out_3 | and_2_out | or_1_out | addi_output | shifter_1_out | multiplier_1_out_6;  // OR_Gate or_2, 16 bits wide
endmodule

module Register_File (
  input  [15:0] Write_Data,
  input  [4:0] rs,
  input  [4:0] rt,
  input  [4:0] rd,
  input  reset,
  input  Clock,
  input  RegWrite,
  output [15:0] data1__rs,
  output [15:0] data2__rt
);

  wire and_1_out, and_2_out, and_3_out, and_4_out, and_5_out, and_6_out, and_7_out, and_8_out, and_9_out,
       and_10_out, and_11_out, and_12_out, and_13_out, and_14_out, and_15_out, and_16_out, and_17_out,
       and_18_out, and_19_out, and_20_out, and_21_out, and_22_out, and_23_out, and_24_out, and_25_out,
       and_26_out, and_27_out, and_28_out, and_29_out, and_30_out, and_31_out, and_32_out, decoder_1_out0,
       decoder_1_out1, decoder_2_out0, decoder_2_out1, decoder_2_out2, decoder_2_out3, decoder_2_out4,
       decoder_2_out5, decoder_2_out6, decoder_2_out7, decoder_2_out8, decoder_2_out9, decoder_2_out10,
       decoder_2_out11, decoder_2_out12, decoder_2_out13, decoder_2_out14, decoder_2_out15, decoder_3_out0,
       decoder_3_out1, decoder_3_out2, decoder_3_out3, decoder_3_out4, decoder_3_out5, decoder_3_out6,
       decoder_3_out7, decoder_3_out8, decoder_3_out9, decoder_3_out10, decoder_3_out11, decoder_3_out12,
       decoder_3_out14, decoder_3_out15;
  wire [15:0] register_1_q, register_2_q, register_3_q, register_4_q, register_5_q, register_6_q,
       register_7_q, register_8_q, register_9_q, register_10_q, register_11_q, register_12_q, register_13_q,
       register_14_q, register_15_q, register_16_q, register_17_q, register_18_q, register_19_q,
       register_20_q, register_21_q, register_22_q, register_23_q, register_24_q, register_25_q,
       register_27_q, register_29_q, register_30_q, register_31_q, register_32_q;

  Decoder #(.enable("false")) decoder_1 (.out0(decoder_1_out0), .out1(decoder_1_out1), .sel(rd[4]));
  Decoder #(.select(4)) decoder_2 (
    .out0(decoder_2_out0), .out1(decoder_2_out1), .out2(decoder_2_out2), .out3(decoder_2_out3),
    .out4(decoder_2_out4), .out5(decoder_2_out5), .out6(decoder_2_out6), .out7(decoder_2_out7),
    .out8(decoder_2_out8), .out9(decoder_2_out9), .out10(decoder_2_out10), .out11(decoder_2_out11),
    .out12(decoder_2_out12), .out13(decoder_2_out13), .out14(decoder_2_out14), .out15(decoder_2_out15),
    .sel(rd[3:0]), .en(decoder_1_out0));
  Pull_Resistor pull_resistor_1 (.node(decoder_2_out1));
  Pull_Resistor pull_resistor_2 (.node(decoder_2_out4));
  Pull_Resistor pull_resistor_3 (.node(decoder_2_out0));
  Pull_Resistor pull_resistor_4 (.node(decoder_2_out2));
  Pull_Resistor pull_resistor_5 (.node(decoder_2_out3));
  Decoder #(.select(4)) decoder_3 (
    .out0(decoder_3_out0), .out1(decoder_3_out1), .out2(decoder_3_out2), .out3(decoder_3_out3),
    .out4(decoder_3_out4), .out5(decoder_3_out5), .out6(decoder_3_out6), .out7(decoder_3_out7),
    .out8(decoder_3_out8), .out9(decoder_3_out9), .out10(decoder_3_out10), .out11(decoder_3_out11),
    .out12(decoder_3_out12), .out13(decoder_3_out12), .out14(decoder_3_out14), .out15(decoder_3_out15),
    .sel(rd[3:0]), .en(decoder_1_out1));
  Pull_Resistor pull_resistor_6 (.node(decoder_3_out1));
  Pull_Resistor pull_resistor_7 (.node(decoder_3_out3));
  Pull_Resistor pull_resistor_8 (.node(decoder_3_out0));
  Pull_Resistor pull_resistor_9 (.node(decoder_3_out2));
  Pull_Resistor pull_resistor_10 (.node(decoder_3_out4));
  Pull_Resistor pull_resistor_11 (.node(decoder_2_out8));
  Pull_Resistor pull_resistor_12 (.node(decoder_2_out11));
  Pull_Resistor pull_resistor_13 (.node(decoder_2_out10));
  Pull_Resistor pull_resistor_14 (.node(decoder_2_out7));
  Pull_Resistor pull_resistor_15 (.node(decoder_2_out5));
  Pull_Resistor pull_resistor_16 (.node(decoder_2_out9));
  Pull_Resistor pull_resistor_17 (.node(decoder_2_out12));
  Pull_Resistor pull_resistor_18 (.node(decoder_2_out6));
  Pull_Resistor pull_resistor_19 (.node(decoder_3_out10));
  Pull_Resistor pull_resistor_20 (.node(decoder_3_out7));
  Pull_Resistor pull_resistor_21 (.node(decoder_3_out12));
  Pull_Resistor pull_resistor_22 (.node(decoder_3_out6));
  Pull_Resistor pull_resistor_23 (.node(decoder_3_out11));
  Pull_Resistor pull_resistor_24 (.node(decoder_3_out9));
  Pull_Resistor pull_resistor_25 (.node(decoder_3_out5));
  Pull_Resistor pull_resistor_26 (.node(decoder_3_out8));
  Pull_Resistor pull_resistor_27 (.node(decoder_2_out13));
  Pull_Resistor pull_resistor_28 (.node(decoder_2_out14));
  Pull_Resistor pull_resistor_29 (.node(decoder_2_out15));
  Pull_Resistor pull_resistor_30 (.node(decoder_3_out12));
  Pull_Resistor pull_resistor_31 (.node(decoder_3_out14));
  Pull_Resistor pull_resistor_32 (.node(decoder_3_out15));
  and and_1 (and_1_out, decoder_2_out0, RegWrite);
  and and_2 (and_2_out, decoder_2_out4, RegWrite);
  and and_3 (and_3_out, decoder_2_out8, RegWrite);
  and and_4 (and_4_out, decoder_2_out12, RegWrite);
  and and_5 (and_5_out, decoder_3_out0, RegWrite);
  and and_6 (and_6_out, decoder_3_out4, RegWrite);
  and and_7 (and_7_out, decoder_3_out8, RegWrite);
  and and_8 (and_8_out, decoder_3_out12, RegWrite);
  Register #(.width(16)) register_1 (.D(Write_Data), .en(and_1_out), .Q(register_1_q), .clk(Clock), .clr(reset));
  Register #(.width(16)) register_2 (.D(Write_Data), .en(and_2_out), .Q(register_2_q), .clk(Clock), .clr(reset));
  Register #(.width(16)) register_3 (.D(Write_Data), .en(and_3_out), .Q(register_3_q), .clk(Clock), .clr(reset));
  Register #(.width(16)) register_4 (.D(Write_Data), .en(and_4_out), .Q(register_4_q), .clk(Clock), .clr(reset));
  Register #(.width(16)) register_5 (.D(Write_Data), .en(and_5_out), .Q(register_5_q), .clk(Clock), .clr(reset));
  Register #(.width(16)) register_6 (.D(Write_Data), .en(and_6_out), .Q(register_6_q), .clk(Clock), .clr(reset));
  Register #(.width(16)) register_7 (.D(Write_Data), .en(and_7_out), .Q(register_7_q), .clk(Clock), .clr(reset));
  Register #(.width(16)) register_8 (.D(Write_Data), .en(and_8_out), .Q(register_8_q), .clk(Clock), .clr(reset));
  and and_9 (and_9_out, decoder_2_out1, RegWrite);
  and and_10 (and_10_out, decoder_2_out5, RegWrite);
  and and_11 (and_11_out, decoder_2_out9, RegWrite);
  and and_12 (and_12_out, decoder_2_out13, RegWrite);
  and and_13 (and_13_out, decoder_3_out1, RegWrite);
  and and_14 (and_14_out, decoder_3_out5, RegWrite);
  and and_15 (and_15_out, decoder_3_out9, RegWrite);
  and and_16 (and_16_out, decoder_3_out12, RegWrite);
  Register #(.width(16)) register_9 (.D(Write_Data), .en(and_9_out), .Q(register_9_q), .clk(Clock), .clr(reset));
  Register #(.width(16)) register_10 (.D(Write_Data), .en(and_10_out), .Q(register_10_q), .clk(Clock), .clr(reset));
  Register #(.width(16)) register_11 (.D(Write_Data), .en(and_11_out), .Q(register_11_q), .clk(Clock), .clr(reset));
  Register #(.width(16)) register_12 (.D(Write_Data), .en(and_12_out), .Q(register_12_q), .clk(Clock), .clr(reset));
  Register #(.width(16)) register_13 (.D(Write_Data), .en(and_13_out), .Q(register_13_q), .clk(Clock), .clr(reset));
  Register #(.width(16)) register_14 (.D(Write_Data), .en(and_14_out), .Q(register_14_q), .clk(Clock), .clr(reset));
  Register #(.width(16)) register_15 (.D(Write_Data), .en(and_15_out), .Q(register_15_q), .clk(Clock), .clr(reset));
  Register #(.width(16)) register_16 (.D(Write_Data), .en(and_16_out), .Q(register_16_q), .clk(Clock), .clr(reset));
  and and_17 (and_17_out, decoder_2_out2, RegWrite);
  and and_18 (and_18_out, decoder_2_out6, RegWrite);
  and and_19 (and_19_out, decoder_2_out10, RegWrite);
  and and_20 (and_20_out, decoder_2_out14, RegWrite);
  and and_21 (and_21_out, decoder_3_out2, RegWrite);
  and and_22 (and_22_out, decoder_3_out6, RegWrite);
  and and_23 (and_23_out, decoder_3_out10, RegWrite);
  and and_24 (and_24_out, decoder_3_out14, RegWrite);
  Register #(.width(16)) register_17 (.D(Write_Data), .en(and_17_out), .Q(register_17_q), .clk(Clock), .clr(reset));
  Register #(.width(16)) register_18 (.D(Write_Data), .en(and_18_out), .Q(register_18_q), .clk(Clock), .clr(reset));
  Register #(.width(16)) register_19 (.D(Write_Data), .en(and_19_out), .Q(register_19_q), .clk(Clock), .clr(reset));
  Register #(.width(16)) register_20 (.D(Write_Data), .en(and_20_out), .Q(register_20_q), .clk(Clock), .clr(reset));
  Register #(.width(16)) register_21 (.D(Write_Data), .en(and_21_out), .Q(register_21_q), .clk(Clock), .clr(reset));
  Register #(.width(16)) register_22 (.D(Write_Data), .en(and_22_out), .Q(register_22_q), .clk(Clock), .clr(reset));
  Register #(.width(16)) register_23 (.D(Write_Data), .en(and_23_out), .Q(register_23_q), .clk(Clock), .clr(reset));
  Register #(.width(16)) register_24 (.D(Write_Data), .en(and_24_out), .Q(register_24_q), .clk(Clock), .clr(reset));
  and and_25 (and_25_out, decoder_2_out3, RegWrite);
  and and_26 (and_26_out, decoder_2_out7, RegWrite);
  and and_27 (and_27_out, decoder_2_out11, RegWrite);
  and and_28 (and_28_out, decoder_2_out15, RegWrite);
  and and_29 (and_29_out, decoder_3_out3, RegWrite);
  and and_30 (and_30_out, decoder_3_out7, RegWrite);
  and and_31 (and_31_out, decoder_3_out11, RegWrite);
  and and_32 (and_32_out, decoder_3_out15, RegWrite);
  Register #(.width(16)) register_25 (.D(Write_Data), .en(and_25_out), .Q(register_25_q), .clk(Clock), .clr(reset));
  Register #(.width(16)) register_26 (.D(Write_Data), .en(and_26_out), .Q(register_3_q), .clk(Clock), .clr(reset));
  Register #(.width(16)) register_27 (.D(Write_Data), .en(and_27_out), .Q(register_27_q), .clk(Clock), .clr(reset));
  Register #(.width(16)) register_28 (.D(Write_Data), .en(and_28_out), .Q(register_20_q), .clk(Clock), .clr(reset));
  Register #(.width(16)) register_29 (.D(Write_Data), .en(and_29_out), .Q(register_29_q), .clk(Clock), .clr(reset));
  Register #(.width(16)) register_30 (.D(Write_Data), .en(and_30_out), .Q(register_30_q), .clk(Clock), .clr(reset));
  Register #(.width(16)) register_31 (.D(Write_Data), .en(and_31_out), .Q(register_31_q), .clk(Clock), .clr(reset));
  Register #(.width(16)) register_32 (.D(Write_Data), .en(and_32_out), .Q(register_32_q), .clk(Clock), .clr(reset));
  Multiplexer #(.select(5), .width(16), .enable("false")) multiplexer_1 (
    .in0(register_1_q), .in1(register_9_q), .in2(register_17_q), .in3(register_25_q), .in4(register_2_q),
    .in5(register_10_q), .in6(register_18_q), .in7(register_3_q), .in8(register_3_q), .in9(register_11_q),
    .in10(register_19_q), .in11(register_27_q), .in12(register_4_q), .in13(register_12_q),
    .in14(register_20_q), .in15(register_20_q), .in16(register_5_q), .in17(register_13_q),
    .in18(register_21_q), .in19(register_29_q), .in20(register_6_q), .in21(register_14_q),
    .in22(register_22_q), .in23(register_30_q), .in24(register_7_q), .in25(register_15_q),
    .in26(register_23_q), .in27(register_31_q), .in28(register_8_q), .in29(register_16_q),
    .in30(register_24_q), .in31(register_32_q), .out(data1__rs), .sel(rs));
  Multiplexer #(.select(5), .width(16), .enable("false")) multiplexer_2 (
    .in0(register_1_q), .in1(register_9_q), .in2(register_17_q), .in3(register_25_q), .in4(register_2_q),
    .in5(register_10_q), .in6(register_18_q), .in7(register_3_q), .in8(register_3_q), .in9(register_11_q),
    .in10(register_19_q), .in11(register_27_q), .in12(register_4_q), .in13(register_12_q),
    .in14(register_20_q), .in15(register_20_q), .in16(register_5_q), .in17(register_13_q),
    .in18(register_21_q), .in19(register_29_q), .in20(register_6_q), .in21(register_14_q),
    .in22(register_22_q), .in23(register_30_q), .in24(register_7_q), .in25(register_15_q),
    .in26(register_23_q), .in27(register_31_q), .in28(register_8_q), .in29(register_16_q),
    .in30(register_24_q), .in31(register_32_q), .out(data2__rt), .sel(rt));
endmodule
